// Logisim project processeur_ARO2_p2_Christopher_Ristic_Julien_Holzer.circ as structural Verilog: 30 circuits, main circuit main
module main (
);

  wire clk, high_write_en_s, low_write_en_s, processeur_aro2_1_memory_high_byte_o,
       processeur_aro2_1_memory_ldr_data, processeur_aro2_1_memory_low_byte_o,
       processeur_aro2_1_memory_str_data_o, RESET_out, sysclk;
  wire [0:0] processeur_aro2_1_instr_addr_o;
  wire [7:0] memory_controller_1_high_data_o, memory_controller_1_low_data_o, ram_1_dout, ram_2_dout;
  wire [14:0] memory_addr_s, processeur_aro2_1_instr_addr_o_2;
  wire [15:0] processeur_aro2_1_memory_wr_data_o, rd_data_s, rom_1_data;

  // Probe on processeur_aro2_1_instr_addr_o_2
  Button RESET (.out(RESET_out));
  Clock #(.highDuration(4), .lowDuration(4)) u_clk (.out(clk));
  Clock u_sysclk (.out(sysclk));
  ROM #(.addrWidth(15), .dataWidth(16)) rom_1 (.addr(processeur_aro2_1_instr_addr_o_2), .data(rom_1_data));
  // Probe on rom_1_data
  processeur_ARO2 processeur_aro2_1 (
    .instr_data_i(rom_1_data), .memory_rd_data_i(rd_data_s), .rst_i(RESET_out), .clk_i(clk),
    .instr_addr_o({processeur_aro2_1_instr_addr_o_2, processeur_aro2_1_instr_addr_o[0]}),
    .memory_addr_o(memory_addr_s), .memory_wr_data_o(processeur_aro2_1_memory_wr_data_o),
    .memory_str_data_o(processeur_aro2_1_memory_str_data_o),
    .memory_ldr_data(processeur_aro2_1_memory_ldr_data),
    .memory_high_byte_o(processeur_aro2_1_memory_high_byte_o),
    .memory_low_byte_o(processeur_aro2_1_memory_low_byte_o));
  // Probe on processeur_aro2_1_memory_wr_data_o
  memory_controller memory_controller_1 (
    .wr_data_i(processeur_aro2_1_memory_wr_data_o), .str_data_i(processeur_aro2_1_memory_str_data_o),
    .ldr_data_i(processeur_aro2_1_memory_ldr_data), .high_byte_i(processeur_aro2_1_memory_high_byte_o),
    .low_byte_i(processeur_aro2_1_memory_low_byte_o), .rd_data_high_i(ram_1_dout),
    .rd_data_low_i(ram_2_dout), .rd_data_o(rd_data_s), .high_data_o(memory_controller_1_high_data_o),
    .low_data_o(memory_controller_1_low_data_o), .high_write_en_o(high_write_en_s),
    .low_write_en_o(low_write_en_s));
  // Probe on memory_controller_1_high_data_o
  // Probe on memory_controller_1_low_data_o
  // Probe on memory_addr_s
  // Probe on memory_addr_s
  RAM #(.addrWidth(15), .databus("bibus")) ram_1 (
    .addr(memory_addr_s), .we(high_write_en_s), .oe(1'b1), .clk(sysclk),
    .din(memory_controller_1_high_data_o), .dout(ram_1_dout));
  RAM #(.addrWidth(15), .databus("bibus")) ram_2 (
    .addr(memory_addr_s), .we(low_write_en_s), .oe(1'b1), .clk(sysclk), .din(memory_controller_1_low_data_o),
    .dout(ram_2_dout));

  // Notes on the sheet:
  //   Attention, votre version de Logisim
  //   ne contient pas de tracker. Si vous
  //   enregistrez votre projet, toutes les
  //   informations du tracker seront
  //   définitivement effacées.
  //   contents of rom_1 (hex, n*v repeats v):
  //   203e 2103 46c0 46c0 22cb 1843 1c93 46c0 1a51 8083 8101 5*46c0
endmodule

module processeur_ARO2 (
  input  [15:0] instr_data_i,
  input  [15:0] memory_rd_data_i,
  input  rst_i,
  input  clk_i,
  output [15:0] instr_addr_o,
  output [14:0] memory_addr_o,
  output [15:0] memory_wr_data_o,
  output memory_str_data_o,
  output memory_ldr_data,
  output memory_high_byte_o,
  output memory_low_byte_o
);

  wire decode_1_decode_en_o, decode_1_link_en_o, decode_execute_reg_1_link_en_o, exec_branch_s,
       execute_1_branch_o, execute_1_execute_en_o, execute_1_link_en_o, execute_en_s,
       execute_memory_reg_1_link_en_o, fetch_1_branch_o, fetch_decode_reg_1_branch_o, fetch_en_s,
       mem_access_en_s, mem_branch_s, mem_link_en_s, memory_access_1_link_en_o, reg_bank_en_s;
  wire [1:0] decode_1_reg_bank_control_bus_o, decode_1_sel_op1_forward_o, decode_1_sel_op2_forward_o,
       decode_1_sel_op_mem_forward_o, decode_execute_reg_1_reg_bank_control_bus_o,
       decode_execute_reg_1_sel_op1_forward_o, decode_execute_reg_1_sel_op2_forward_o,
       decode_execute_reg_1_sel_op_mem_forward_o, execute_1_reg_bank_ctl_bus_o,
       execute_memory_reg_1_reg_bank_ctl_bus_o, mem_reg_bank_ctl_s, memory_access_1_reg_bank_ctl_bus_o;
  wire [2:0] decode_1_adr_reg_d_o, decode_1_adr_reg_m_o, decode_1_adr_reg_mem_o, decode_1_adr_reg_n_o,
       decode_1_imm3_o, decode_execute_reg_1_adr_reg_d_o, decode_execute_reg_1_imm3_o,
       execute_1_addr_reg_d_o, execute_memory_reg_1_adr_reg_d_o, mem_adr_reg_d_s, memory_access_1_adr_reg_d_o;
  wire [3:0] execute_1_cpsr_o, execute_memory_reg_1_cpsr_o;
  wire [4:0] decode_1_imm5_o, decode_1_mem_control_bus_o, decode_execute_reg_1_imm5_o,
       decode_execute_reg_1_mem_control_bus_o, execute_1_mem_ctl_bus_o, execute_memory_reg_1_mem_ctl_bus_o;
  wire [6:0] decode_1_fetch_control_bus_o, decode_execute_reg_1_fetch_control_bus_o,
       execute_1_fetch_ctl_bus_o, execute_memory_reg_1_fetch_ctl_bus_o;
  wire [7:0] decode_1_imm8_o, decode_1_offset8_o, decode_execute_reg_1_imm_8_o,
       decode_execute_reg_1_offset8_o;
  wire [10:0] decode_1_offset11_o, decode_execute_reg_1_offset11_o;
  wire [14:0] decode_1_execute_control_bus_o, decode_execute_reg_1_execute_control_bus_o;
  wire [15:0] bank_registers_1_pc_pres_o, bank_registers_1_register_m_read_data_o,
       bank_registers_1_register_mem_read_data_o, bank_registers_1_register_n_read_data_o, data_jump_adr_s,
       decode_1_lr_addr_o, decode_execute_reg_1_lr_addr_o, execute_1_data_o, execute_1_lr_addr_o,
       execute_1_reg_mem_read_data_o, execute_memory_reg_1_data_o, execute_memory_reg_1_lr_addr_o,
       execute_memory_reg_1_reg_mem_read_data_o, fetch_1_instr_data_o, fetch_1_lr_addr_o, fetch_1_pc_fut_o,
       fetch_decode_reg_1_instr_data_o, fetch_decode_reg_1_lr_addr_o, mem_LR_adr_s, mem_reg_d_data_s,
       memory_access_1_lr_addr_o, memory_access_1_mem_adr_byte_o;

  // Probe on data_jump_adr_s
  fetch fetch_1 (
    .fetch_en_i(fetch_en_s), .instr_data_i(instr_data_i), .PC_pres_i(bank_registers_1_pc_pres_o),
    .branch_addr_i(data_jump_adr_s), .branch_i(exec_branch_s), .instr_addr_o(instr_addr_o),
    .PC_fut_o(fetch_1_pc_fut_o), .LR_addr_o(fetch_1_lr_addr_o), .instr_data_o(fetch_1_instr_data_o),
    .branch_o(fetch_1_branch_o));
  // Probe on instr_addr_o
  // Probe on fetch_1_pc_fut_o
  // Probe on fetch_1_instr_data_o
  fetch_decode_reg fetch_decode_reg_1 (
    .LR_addr_i(fetch_1_lr_addr_o), .instr_data_i(fetch_1_instr_data_o), .branch_i(fetch_1_branch_o),
    .fetch_en_i(fetch_en_s), .clk_i(clk_i), .rst_i(rst_i), .LR_addr_o(fetch_decode_reg_1_lr_addr_o),
    .instr_data_o(fetch_decode_reg_1_instr_data_o), .branch_o(fetch_decode_reg_1_branch_o));
  // Probe on fetch_decode_reg_1_instr_data_o
  decode decode_1 (
    .lr_addr_i(fetch_decode_reg_1_lr_addr_o), .instr_data_i(fetch_decode_reg_1_instr_data_o),
    .branch_i(fetch_decode_reg_1_branch_o), .clk_i(clk_i), .rst_i(rst_i), .adr_reg_n_o(decode_1_adr_reg_n_o),
    .adr_reg_m_o(decode_1_adr_reg_m_o), .adr_reg_mem_o(decode_1_adr_reg_mem_o),
    .adr_reg_d_o(decode_1_adr_reg_d_o), .imm3_o(decode_1_imm3_o), .imm5_o(decode_1_imm5_o),
    .offset11_o(decode_1_offset11_o), .offset8_o(decode_1_offset8_o), .imm8_o(decode_1_imm8_o),
    .lr_addr_o(decode_1_lr_addr_o), .fetch_control_bus_o(decode_1_fetch_control_bus_o),
    .execute_control_bus_o(decode_1_execute_control_bus_o), .mem_control_bus_o(decode_1_mem_control_bus_o),
    .reg_bank_control_bus_o(decode_1_reg_bank_control_bus_o), .fetch_en_o(fetch_en_s),
    .decode_en_o(decode_1_decode_en_o), .execute_en_o(execute_en_s), .memory_access_en_o(mem_access_en_s),
    .reg_bank_en_o(reg_bank_en_s), .link_en_o(decode_1_link_en_o),
    .sel_op1_forward_o(decode_1_sel_op1_forward_o), .sel_op2_forward_o(decode_1_sel_op2_forward_o),
    .sel_op_mem_forward_o(decode_1_sel_op_mem_forward_o));
  // Probe on decode_1_adr_reg_d_o
  // Probe on mem_reg_d_data_s
  bank_registers bank_registers_1 (
    .register_d_sel_i(mem_adr_reg_d_s), .register_d_data_i(mem_reg_d_data_s),
    .register_n_sel_i(decode_1_adr_reg_n_o), .register_m_sel_i(decode_1_adr_reg_m_o),
    .register_mem_sel_i(decode_1_adr_reg_mem_o), .reg_bank_control_bus_i(mem_reg_bank_ctl_s),
    .PC_fut_i(fetch_1_pc_fut_o), .LR_addr_i(mem_LR_adr_s), .branch_i(mem_branch_s),
    .link_en_i(mem_link_en_s), .bank_reg_en_i(reg_bank_en_s), .clk_i(clk_i), .rst_i(rst_i),
    .PC_pres_o(bank_registers_1_pc_pres_o), .register_n_read_data_o(bank_registers_1_register_n_read_data_o),
    .register_m_read_data_o(bank_registers_1_register_m_read_data_o),
    .register_mem_read_data_o(bank_registers_1_register_mem_read_data_o));
  decode_execute_reg decode_execute_reg_1 (
    .adr_reg_d_i(decode_1_adr_reg_d_o), .imm3_i(decode_1_imm3_o), .imm5_i(decode_1_imm5_o),
    .offset11_i(decode_1_offset11_o), .offset8_i(decode_1_offset8_o), .imm8_i(decode_1_imm8_o),
    .LR_addr_i(decode_1_lr_addr_o), .fetch_control_bus_i(decode_1_fetch_control_bus_o),
    .execute_control_bus_i(decode_1_execute_control_bus_o), .mem_control_bus_i(decode_1_mem_control_bus_o),
    .reg_bank_control_bus_i(decode_1_reg_bank_control_bus_o), .decode_en_i(decode_1_decode_en_o),
    .link_en_i(decode_1_link_en_o), .sel_op1_forward_i(decode_1_sel_op1_forward_o),
    .sel_op2_forward_i(decode_1_sel_op2_forward_o), .sel_op_mem_forward_i(decode_1_sel_op_mem_forward_o),
    .clk_i(clk_i), .rst_i(rst_i), .adr_reg_d_o(decode_execute_reg_1_adr_reg_d_o),
    .imm3_o(decode_execute_reg_1_imm3_o), .imm5_o(decode_execute_reg_1_imm5_o),
    .offset11_o(decode_execute_reg_1_offset11_o), .offset8_o(decode_execute_reg_1_offset8_o),
    .imm_8_o(decode_execute_reg_1_imm_8_o), .LR_addr_o(decode_execute_reg_1_lr_addr_o),
    .fetch_control_bus_o(decode_execute_reg_1_fetch_control_bus_o),
    .execute_control_bus_o(decode_execute_reg_1_execute_control_bus_o),
    .mem_control_bus_o(decode_execute_reg_1_mem_control_bus_o),
    .reg_bank_control_bus_o(decode_execute_reg_1_reg_bank_control_bus_o),
    .link_en_o(decode_execute_reg_1_link_en_o), .sel_op1_forward_o(decode_execute_reg_1_sel_op1_forward_o),
    .sel_op2_forward_o(decode_execute_reg_1_sel_op2_forward_o),
    .sel_op_mem_forward_o(decode_execute_reg_1_sel_op_mem_forward_o));
  // Probe on decode_execute_reg_1_adr_reg_d_o
  // Probe on bank_registers_1_pc_pres_o
  execute execute_1 (
    .reg_data_n_i(bank_registers_1_register_n_read_data_o),
    .reg_data_m_i(bank_registers_1_register_m_read_data_o),
    .reg_mem_read_data_i(bank_registers_1_register_mem_read_data_o),
    .addr_reg_d_i(decode_execute_reg_1_adr_reg_d_o), .imm3(decode_execute_reg_1_imm3_o),
    .imm5(decode_execute_reg_1_imm5_o), .offset_incond(decode_execute_reg_1_offset11_o),
    .offset_cond(decode_execute_reg_1_offset8_o), .imm8(decode_execute_reg_1_imm_8_o),
    .lr_addr_i(decode_execute_reg_1_lr_addr_o), .fetch_ctl_bus_i(decode_execute_reg_1_fetch_control_bus_o),
    .execute_control_bus(decode_execute_reg_1_execute_control_bus_o),
    .mem_ctl_bus_i(decode_execute_reg_1_mem_control_bus_o),
    .reg_bank_ctl_bus_i(decode_execute_reg_1_reg_bank_control_bus_o),
    .link_en_i(decode_execute_reg_1_link_en_o), .sel_op1_forward_i(decode_execute_reg_1_sel_op1_forward_o),
    .sel_op2_forward_i(decode_execute_reg_1_sel_op2_forward_o),
    .sel_op_mem_forward_i(decode_execute_reg_1_sel_op_mem_forward_o), .execute_en_i(execute_en_s),
    .memory_data_out_i(mem_reg_d_data_s), .execute_data_out_i(execute_memory_reg_1_data_o), .clk_i(clk_i),
    .rst_i(rst_i), .data_o(execute_1_data_o), .cpsr_o(execute_1_cpsr_o),
    .addr_reg_d_o(execute_1_addr_reg_d_o), .fetch_ctl_bus_o(execute_1_fetch_ctl_bus_o),
    .mem_ctl_bus_o(execute_1_mem_ctl_bus_o), .reg_bank_ctl_bus_o(execute_1_reg_bank_ctl_bus_o),
    .lr_addr_o(execute_1_lr_addr_o), .link_en_o(execute_1_link_en_o),
    .reg_mem_read_data_o(execute_1_reg_mem_read_data_o), .execute_en_o(execute_1_execute_en_o),
    .branch_o(execute_1_branch_o));
  // Probe on execute_1_addr_reg_d_o
  // Probe on execute_1_reg_mem_read_data_o
  // Probe on execute_memory_reg_1_adr_reg_d_o
  execute_memory_reg execute_memory_reg_1 (
    .data_i(execute_1_data_o), .cpsr_i(execute_1_cpsr_o), .adr_reg_d_i(execute_1_addr_reg_d_o),
    .fetch_ctl_bus_i(execute_1_fetch_ctl_bus_o), .mem_ctl_bus_i(execute_1_mem_ctl_bus_o),
    .reg_bank_ctl_bus_i(execute_1_reg_bank_ctl_bus_o), .lr_addr_i(execute_1_lr_addr_o),
    .link_en_i(execute_1_link_en_o), .reg_mem_read_data_i(execute_1_reg_mem_read_data_o),
    .execute_en_i(execute_1_execute_en_o), .branch_i(execute_1_branch_o), .clk_i(clk_i), .rst_i(rst_i),
    .data_o(execute_memory_reg_1_data_o), .cpsr_o(execute_memory_reg_1_cpsr_o),
    .adr_reg_d_o(execute_memory_reg_1_adr_reg_d_o), .fetch_ctl_bus_o(execute_memory_reg_1_fetch_ctl_bus_o),
    .mem_ctl_bus_o(execute_memory_reg_1_mem_ctl_bus_o),
    .reg_bank_ctl_bus_o(execute_memory_reg_1_reg_bank_ctl_bus_o), .lr_addr_o(execute_memory_reg_1_lr_addr_o),
    .link_en_o(execute_memory_reg_1_link_en_o),
    .reg_mem_read_data_o(execute_memory_reg_1_reg_mem_read_data_o), .branch_o(exec_branch_s));
  // Probe on memory_rd_data_i
  memory_access memory_access_1 (
    .mem_data_i(memory_rd_data_i), .data_i(execute_memory_reg_1_data_o),
    .cpsr_i(execute_memory_reg_1_cpsr_o), .addr_reg_d_i(execute_memory_reg_1_adr_reg_d_o),
    .fetch_ctl_bus_i(execute_memory_reg_1_fetch_ctl_bus_o),
    .mem_ctl_bus_i(execute_memory_reg_1_mem_ctl_bus_o),
    .reg_bank_ctl_bus_i(execute_memory_reg_1_reg_bank_ctl_bus_o), .lr_addr_i(execute_memory_reg_1_lr_addr_o),
    .link_en_i(execute_memory_reg_1_link_en_o),
    .reg_mem_read_data_i(execute_memory_reg_1_reg_mem_read_data_o), .memory_access_en_i(mem_access_en_s),
    .rst_i(clk_i), .clk_i(rst_i), .mem_data_adr_o(memory_addr_o),
    .mem_adr_byte_o(memory_access_1_mem_adr_byte_o), .mem_data_out_o(memory_wr_data_o),
    .str_data_o(memory_str_data_o), .ldr_data_o(memory_ldr_data), .high_byte_o(memory_high_byte_o),
    .low_byte_o(memory_low_byte_o), .mem_out_o(data_jump_adr_s), .adr_reg_d_o(memory_access_1_adr_reg_d_o),
    .reg_bank_ctl_bus_o(memory_access_1_reg_bank_ctl_bus_o), .link_en_o(memory_access_1_link_en_o),
    .lr_addr_o(memory_access_1_lr_addr_o), .branch_o(mem_branch_s));
  // Probe on memory_access_1_mem_adr_byte_o
  // Probe on memory_wr_data_o
  memory_bank_reg memory_bank_reg_1 (
    .mem_out_i(data_jump_adr_s), .addr_reg_d_i(memory_access_1_adr_reg_d_o),
    .reg_bank_ctl_bus_i(memory_access_1_reg_bank_ctl_bus_o), .link_en_i(memory_access_1_link_en_o),
    .ldr_addr_i(memory_access_1_lr_addr_o), .memory_access_en_i(mem_access_en_s), .clk_i(clk_i),
    .rst_i(rst_i), .mem_out_o(mem_reg_d_data_s), .addr_reg_d_o(mem_adr_reg_d_s),
    .reg_bank_ctl_bus_o(mem_reg_bank_ctl_s), .link_en_o(mem_link_en_s), .ldr_addr_o(mem_LR_adr_s));

  // Other names for the same wires on the sheet: clk_s = clk_i; instr_addr_s[15:0] = instr_addr_o;
  //   instr_data_s[15:0] = instr_data_i; memory_rd_data_s[15:0] = memory_rd_data_i; rst_s = rst_i

  // Notes on the sheet:
  //   Attention, votre version de Logisim
  //   ne contient pas de tracker. Si vous
  //   enregistrez votre projet, toutes les
  //   informations du tracker seront
  //   définitivement effacées.
  //   Memory interface inputs
  //   Standard inputs
  //   Instruction memory outputs
  //   Memory interface outputs
  //   Processeur ARO2
endmodule

module memory_controller (
  input  [15:0] wr_data_i,
  input  str_data_i,
  input  ldr_data_i,
  input  high_byte_i,
  input  low_byte_i,
  input  [7:0] rd_data_high_i,
  input  [7:0] rd_data_low_i,
  output [15:0] rd_data_o,
  output [7:0] high_data_o,
  output [7:0] low_data_o,
  output high_write_en_o,
  output low_write_en_o
);

  wire and_3_out, and_4_out, and_5_out, not_1_out;
  wire [7:0] multiplexer_2_out, multiplexer_3_out;

  and and_1 (low_write_en_o, low_byte_i, str_data_i);
  and and_2 (high_write_en_o, high_byte_i, str_data_i);
  and and_3 (and_3_out, low_byte_i, high_byte_i);
  and and_4 (and_4_out, high_byte_i, ~low_byte_i);  // AND_Gate
  and and_5 (and_5_out, high_byte_i, low_byte_i);
  not not_1 (not_1_out, and_5_out);
  Multiplexer #(.width(8), .enable("false")) multiplexer_1 (
    .in0(wr_data_i[7:0]), .in1(wr_data_i[15:8]), .out(high_data_o), .sel(and_3_out));
  Multiplexer #(.width(8), .enable("false")) multiplexer_2 (
    .in0(rd_data_low_i), .in1(rd_data_high_i), .out(multiplexer_2_out), .sel(and_4_out));
  Multiplexer #(.width(8), .enable("false")) multiplexer_3 (
    .in0(rd_data_high_i), .in1({8{1'b0}}), .out(multiplexer_3_out), .sel(not_1_out));
  assign rd_data_o = ldr_data_i ? {multiplexer_3_out, multiplexer_2_out} : 16'bz;  // Controlled_Buffer controlled_buffer_1

  assign low_data_o = wr_data_i[7:0];

  // Other names for the same wires on the sheet: wr_data_high_o[7:0] = high_data_o;
  //   wr_data_low_o[7:0] = wr_data_i[7:0]

  // Notes on the sheet:
  //   Attention, votre version de Logisim
  //   ne contient pas de tracker. Si vous
  //   enregistrez votre projet, toutes les
  //   informations du tracker seront
  //   définitivement effacées.
  //   Write interface
  //   Read interface
endmodule

module fetch (
  input  fetch_en_i,
  input  [15:0] instr_data_i,
  input  [15:0] PC_pres_i,
  input  [15:0] branch_addr_i,
  input  branch_i,
  output [15:0] instr_addr_o,
  output [15:0] PC_fut_o,
  output [15:0] LR_addr_o,
  output [15:0] instr_data_o,
  output branch_o
);

  wire or_1_out;
  wire [15:0] multiplexer_2_out;

  Multiplexer #(.enable("false")) multiplexer_1 (.in0(1'b0), .in1(branch_i), .out(branch_o), .sel(fetch_en_i));
  Adder #(.width(16)) adder_1 (.a(PC_pres_i), .b(16'h2), .out(LR_addr_o), .cin(1'b0));  // open: cout
  Multiplexer #(.width(16), .enable("false")) multiplexer_2 (
    .in0(LR_addr_o), .in1(branch_addr_i), .out(multiplexer_2_out), .sel(branch_i));
  Multiplexer #(.width(16), .enable("false")) multiplexer_3 (
    .in0(PC_pres_i), .in1(multiplexer_2_out), .out(PC_fut_o), .sel(or_1_out));
  or or_1 (or_1_out, fetch_en_i, branch_i);

  assign instr_addr_o = PC_pres_i;
  assign instr_data_o = instr_data_i;

  // Other names for the same wires on the sheet: branch_addr_s[15:0] = branch_addr_i; branch_s = branch_i;
  //   fetch_en_s = fetch_en_i; instr_data_s[15:0] = instr_data_i; PC_pres_s[15:0] = PC_pres_i

  // Notes on the sheet:
  //   Attention, votre version de Logisim
  //   ne contient pas de tracker. Si vous
  //   enregistrez votre projet, toutes les
  //   informations du tracker seront
  //   définitivement effacées.
  //   Increment du PC
  //   L'état de PC va directement sur l'adresse d'instruction
endmodule

module fetch_decode_reg (
  input  [15:0] LR_addr_i,
  input  [15:0] instr_data_i,
  input  branch_i,
  input  fetch_en_i,
  input  clk_i,
  input  rst_i,
  output [15:0] LR_addr_o,
  output [15:0] instr_data_o,
  output branch_o
);

  wire multiplexer_1_out;

  Multiplexer #(.enable("false")) multiplexer_1 (.in0(1'b0), .in1(branch_i), .out(multiplexer_1_out), .sel(fetch_en_i));
  Register #(.width(16)) register_1 (.D(LR_addr_i), .en(fetch_en_i), .clk(clk_i), .Q(LR_addr_o), .clr(rst_i));
  Register #(.width(16)) register_2 (.D(instr_data_i), .en(fetch_en_i), .clk(clk_i), .Q(instr_data_o), .clr(rst_i));
  Register #(.width(1)) register_3 (.D(multiplexer_1_out), .en(1'b1), .clk(clk_i), .Q(branch_o), .clr(rst_i));

  // Other names for the same wires on the sheet: clk_s = clk_i; fetch_en_s = fetch_en_i; rst_s = rst_i

  // Notes on the sheet:
  //   Attention, votre version de Logisim
  //   ne contient pas de tracker. Si vous
  //   enregistrez votre projet, toutes les
  //   informations du tracker seront
  //   définitivement effacées.
endmodule

module condition_tester (
  input  cond_en_i,
  input  [3:0] cond_i,
  input  Z_i,
  input  C_i,
  input  N_i,
  input  V_i,
  output cond_test_o
);

  wire and_1_out, and_2_out, comparator_1_eq, not_1_out, not_2_out, not_3_out, not_4_out, not_5_out,
       not_6_out, not_7_out, not_8_out, or_1_out, or_2_out;
  wire [3:0] multiplexer_1_out;

  and and_1 (and_1_out, C_i, not_1_out);
  not not_1 (not_1_out, Z_i);
  not not_2 (not_2_out, C_i);
  or or_1 (or_1_out, not_2_out, Z_i);
  Comparator #(.width(1), .mode("unsigned")) comparator_1 (.a(N_i), .b(V_i), .eq(comparator_1_eq));  // open: gt, lt
  not not_3 (not_3_out, Z_i);
  not not_4 (not_4_out, comparator_1_eq);
  and and_2 (and_2_out, comparator_1_eq, not_3_out);
  or or_2 (or_2_out, not_4_out, Z_i);
  not not_5 (not_5_out, Z_i);
  not not_6 (not_6_out, C_i);
  not not_7 (not_7_out, N_i);
  not not_8 (not_8_out, V_i);
  Multiplexer #(.width(4), .enable("false")) multiplexer_1 (
    .in0(4'b1110), .in1(cond_i), .out(multiplexer_1_out), .sel(cond_en_i));
  Multiplexer #(.select(4), .enable("false")) multiplexer_2 (
    .in0(Z_i), .in1(not_5_out), .in2(C_i), .in3(not_6_out), .in4(N_i), .in5(not_7_out), .in6(V_i),
    .in7(not_8_out), .in8(and_1_out), .in9(or_1_out), .in10(comparator_1_eq), .in11(not_4_out),
    .in12(and_2_out), .in13(or_2_out), .in14(1'b1), .in15(1'b1), .out(cond_test_o), .sel(multiplexer_1_out));

  // Notes on the sheet:
  //   Attention, votre version de Logisim
  //   ne contient pas de tracker. Si vous
  //   enregistrez votre projet, toutes les
  //   informations du tracker seront
  //   définitivement effacées.
  //   Always (Inconditionnel)
endmodule

module decode (
  input  [15:0] lr_addr_i,
  input  [15:0] instr_data_i,
  input  branch_i,
  input  clk_i,
  input  rst_i,
  output [2:0] adr_reg_n_o,
  output [2:0] adr_reg_m_o,
  output [2:0] adr_reg_mem_o,
  output [2:0] adr_reg_d_o,
  output [2:0] imm3_o,
  output [4:0] imm5_o,
  output [10:0] offset11_o,
  output [7:0] offset8_o,
  output [7:0] imm8_o,
  output [15:0] lr_addr_o,
  output [6:0] fetch_control_bus_o,
  output [14:0] execute_control_bus_o,
  output [4:0] mem_control_bus_o,
  output [1:0] reg_bank_control_bus_o,
  output fetch_en_o,
  output decode_en_o,
  output execute_en_o,
  output memory_access_en_o,
  output reg_bank_en_o,
  output link_en_o,
  output [1:0] sel_op1_forward_o,
  output [1:0] sel_op2_forward_o,
  output [1:0] sel_op_mem_forward_o
);

  wire sel_rd_s, sel_rm_s;
  wire [1:0] sel_rn_s;
  wire [2:0] multiplexer_1_out, multiplexer_4_out, rd_2_0_s, rd_10_8_s, rm_8_6_s, rn_5_3_s;
  wire [3:0] cond_s;
  wire [5:5] main_control_unit_1_decode_control_bus_o;

  decode_instr_splitter decode_instr_splitter_1 (
    .instr_i(instr_data_i), .rd_2_0_o(rd_2_0_s), .rd_10_8_o(rd_10_8_s), .rn_5_3_o(rn_5_3_s),
    .rm_8_6_o(rm_8_6_s), .offset3_8_6_o(imm3_o), .offset5_10_6_o(imm5_o), .offset8_7_0_o(imm8_o),
    .offset11_10_0_o(offset11_o), .cond_11_8_o(cond_s));
  main_control_unit main_control_unit_1 (
    .instr_i(instr_data_i), .cond_i(cond_s), .branch_i(branch_i), .adr_reg_d_i(adr_reg_d_o),
    .adr_reg_n_i(adr_reg_n_o), .adr_reg_m_i(adr_reg_m_o), .adr_reg_mem_i(adr_reg_d_o), .clk_i(clk_i),
    .rst_i(rst_i), .fetch_control_bus_o(fetch_control_bus_o),
    .decode_control_bus_o({main_control_unit_1_decode_control_bus_o[5], sel_rd_s, link_en_o, sel_rm_s, sel_rn_s}),
    .execute_control_bus_o(execute_control_bus_o), .mem_control_bus_o(mem_control_bus_o),
    .reg_bank_control_bus_o(reg_bank_control_bus_o), .fetch_en_o(fetch_en_o), .decode_en_o(decode_en_o),
    .execute_en_o(execute_en_o), .memory_access_en_o(memory_access_en_o), .reg_bank_en_o(reg_bank_en_o),
    .sel_op1_forward_o(sel_op1_forward_o), .sel_op2_forward_o(sel_op2_forward_o),
    .sel_op_mem_forward_o(sel_op_mem_forward_o));
  Multiplexer #(.width(3), .enable("false")) multiplexer_1 (
    .in0(rd_2_0_s), .in1(rd_10_8_s), .out(multiplexer_1_out), .sel(sel_rd_s));
  Multiplexer #(.width(3), .enable("false")) multiplexer_2 (
    .in0(rm_8_6_s), .in1(rn_5_3_s), .out(adr_reg_m_o), .sel(sel_rm_s));
  Multiplexer #(.width(3), .enable("false")) multiplexer_3 (
    .in0(multiplexer_1_out), .in1(multiplexer_4_out), .out(adr_reg_d_o), .sel(sel_rn_s[1]));
  Multiplexer #(.width(3), .enable("false")) multiplexer_4 (
    .in0(3'b110), .in1(3'b111), .out(multiplexer_4_out), .sel(sel_rn_s[0]));
  Multiplexer #(.select(2), .width(3), .enable("false")) multiplexer_5 (
    .in0(rn_5_3_s), .in1(adr_reg_d_o), .in2(3'b111), .in3(3'b110), .out(adr_reg_n_o), .sel(sel_rn_s));

  assign adr_reg_mem_o = adr_reg_d_o;
  assign lr_addr_o = lr_addr_i;
  assign offset8_o = imm8_o;

  // Other names for the same wires on the sheet: link_en_s = link_en_o; adr_reg_d_s[2:0] = adr_reg_d_o;
  //   adr_reg_m_s[2:0] = adr_reg_m_o; adr_reg_n_s[2:0] = adr_reg_n_o; branch_s = branch_i; clk_s = clk_i;
  //   lr_addr_s[15:0] = lr_addr_i; offset3_8_6_s[2:0] = imm3_o; offset5_10_6_s[4:0] = imm5_o;
  //   offset8_7_0_s[7:0] = imm8_o; offset11_10_0_s[10:0] = offset11_o; rst_s = rst_i

  // Notes on the sheet:
  //   Attention, votre version de Logisim
  //   ne contient pas de tracker. Si vous
  //   enregistrez votre projet, toutes les
  //   informations du tracker seront
  //   définitivement effacées.
  //   Used for BL msb
  //   Used for BL lsb
  //   Used for BL msb
  //   Used for BL lsb
  //   Management special BL
endmodule

module decode_execute_reg (
  input  [2:0] adr_reg_d_i,
  input  [2:0] imm3_i,
  input  [4:0] imm5_i,
  input  [10:0] offset11_i,
  input  [7:0] offset8_i,
  input  [7:0] imm8_i,
  input  [15:0] LR_addr_i,
  input  [6:0] fetch_control_bus_i,
  input  [14:0] execute_control_bus_i,
  input  [4:0] mem_control_bus_i,
  input  [1:0] reg_bank_control_bus_i,
  input  decode_en_i,
  input  link_en_i,
  input  [1:0] sel_op1_forward_i,
  input  [1:0] sel_op2_forward_i,
  input  [1:0] sel_op_mem_forward_i,
  input  clk_i,
  input  rst_i,
  output [2:0] adr_reg_d_o,
  output [2:0] imm3_o,
  output [4:0] imm5_o,
  output [10:0] offset11_o,
  output [7:0] offset8_o,
  output [7:0] imm_8_o,
  output [15:0] LR_addr_o,
  output [6:0] fetch_control_bus_o,
  output [14:0] execute_control_bus_o,
  output [4:0] mem_control_bus_o,
  output [1:0] reg_bank_control_bus_o,
  output link_en_o,
  output [1:0] sel_op1_forward_o,
  output [1:0] sel_op2_forward_o,
  output [1:0] sel_op_mem_forward_o
);

  wire multiplexer_5_out;
  wire [1:0] multiplexer_4_out;
  wire [4:0] multiplexer_3_out;
  wire [6:0] multiplexer_1_out;
  wire [14:0] multiplexer_2_out;

  Multiplexer #(.width(7), .enable("false")) multiplexer_1 (
    .in0({7{1'b0}}), .in1(fetch_control_bus_i), .out(multiplexer_1_out), .sel(decode_en_i));
  Multiplexer #(.width(15), .enable("false")) multiplexer_2 (
    .in0({15{1'b0}}), .in1(execute_control_bus_i), .out(multiplexer_2_out), .sel(decode_en_i));
  Multiplexer #(.width(5), .enable("false")) multiplexer_3 (
    .in0({5{1'b0}}), .in1(mem_control_bus_i), .out(multiplexer_3_out), .sel(decode_en_i));
  Multiplexer #(.width(2), .enable("false")) multiplexer_4 (
    .in0(2'b00), .in1(reg_bank_control_bus_i), .out(multiplexer_4_out), .sel(decode_en_i));
  Multiplexer #(.enable("false")) multiplexer_5 (
    .in0(1'b0), .in1(link_en_i), .out(multiplexer_5_out), .sel(decode_en_i));
  Register #(.width(3)) register_1 (.D(adr_reg_d_i), .en(decode_en_i), .clk(clk_i), .Q(adr_reg_d_o), .clr(rst_i));
  Register #(.width(3)) register_2 (.D(imm3_i), .en(decode_en_i), .clk(clk_i), .Q(imm3_o), .clr(rst_i));
  Register #(.width(5)) register_3 (.D(imm5_i), .en(decode_en_i), .clk(clk_i), .Q(imm5_o), .clr(rst_i));
  Register #(.width(11)) register_4 (.D(offset11_i), .en(decode_en_i), .clk(clk_i), .Q(offset11_o), .clr(rst_i));
  Register register_5 (.D(offset8_i), .en(decode_en_i), .clk(clk_i), .Q(offset8_o), .clr(rst_i));
  Register register_6 (.D(imm8_i), .en(decode_en_i), .clk(clk_i), .Q(imm_8_o), .clr(rst_i));
  Register #(.width(16)) register_7 (.D(LR_addr_i), .en(decode_en_i), .clk(clk_i), .Q(LR_addr_o), .clr(rst_i));
  Register #(.width(7)) register_8 (
    .D(multiplexer_1_out), .en(1'b1), .clk(clk_i), .Q(fetch_control_bus_o), .clr(rst_i));
  Register #(.width(15)) register_9 (
    .D(multiplexer_2_out), .en(1'b1), .clk(clk_i), .Q(execute_control_bus_o), .clr(rst_i));
  Register #(.width(5)) register_10 (.D(multiplexer_3_out), .en(1'b1), .clk(clk_i), .Q(mem_control_bus_o), .clr(rst_i));
  Register #(.width(2)) register_11 (
    .D(multiplexer_4_out), .en(1'b1), .clk(clk_i), .Q(reg_bank_control_bus_o), .clr(rst_i));
  Register #(.width(1)) register_12 (.D(multiplexer_5_out), .en(1'b1), .clk(clk_i), .Q(link_en_o), .clr(rst_i));
  Register #(.width(2)) register_13 (
    .D(sel_op1_forward_i), .en(decode_en_i), .clk(clk_i), .Q(sel_op1_forward_o), .clr(rst_i));
  Register #(.width(2)) register_14 (
    .D(sel_op2_forward_i), .en(decode_en_i), .clk(clk_i), .Q(sel_op2_forward_o), .clr(rst_i));
  Register #(.width(2)) register_15 (
    .D(sel_op_mem_forward_i), .en(decode_en_i), .clk(clk_i), .Q(sel_op_mem_forward_o), .clr(rst_i));

  // Other names for the same wires on the sheet: clk_s = clk_i; decode_en_s = decode_en_i; rst_s = rst_i

  // Notes on the sheet:
  //   Attention, votre version de Logisim
  //   ne contient pas de tracker. Si vous
  //   enregistrez votre projet, toutes les
  //   informations du tracker seront
  //   définitivement effacées.
endmodule

module bank_registers (
  input  [2:0] register_d_sel_i,
  input  [15:0] register_d_data_i,
  input  [2:0] register_n_sel_i,
  input  [2:0] register_m_sel_i,
  input  [2:0] register_mem_sel_i,
  input  [1:0] reg_bank_control_bus_i,
  input  [15:0] PC_fut_i,
  input  [15:0] LR_addr_i,
  input  branch_i,
  input  link_en_i,
  input  bank_reg_en_i,
  input  clk_i,
  input  rst_i,
  output [15:0] PC_pres_o,
  output [15:0] register_n_read_data_o,
  output [15:0] register_m_read_data_o,
  output [15:0] register_mem_read_data_o
);

  wire and_1_out, bank_wr_validated_s, branch_validated_s, link_en_validated_s, lr_manager_1_out_10;
  wire [7:0] write_en_bus_s;
  wire [15:0] lr_manager_1_out_9, LR_pres, multiplexer_1_out, R0_q, R1_q, R2_q, R3_q, R4_q,
       reg_m_read_data_s, reg_mem_read_data_s, reg_n_read_data_s, SP_pres;

  Demultiplexer #(.select(3), .enable("false")) demultiplexer_1 (
    .out0(write_en_bus_s[0]), .out1(write_en_bus_s[1]), .out2(write_en_bus_s[2]), .out3(write_en_bus_s[3]),
    .out4(write_en_bus_s[4]), .out5(write_en_bus_s[5]), .out6(write_en_bus_s[6]), .out7(write_en_bus_s[7]),
    .in(bank_wr_validated_s), .sel(register_d_sel_i));
  // Probe on register_d_sel_i
  // Probe on LR_addr_i
  LR_manager lr_manager_1 (
    .data_i(register_d_data_i), .pc_fut_lr_i(PC_fut_i), .LR_addr_i(LR_addr_i), .branch_i(branch_validated_s),
    .write_en_i(write_en_bus_s[6]), .link_en_i(link_en_validated_s), .clk_i(clk_i), .rst_i(rst_i),
    .out_9(lr_manager_1_out_9), .out_10(lr_manager_1_out_10));
  // Probe on PC_fut_i
  // Probe on register_d_data_i
  and and_1 (and_1_out, write_en_bus_s[7], ~link_en_i);  // AND_Gate
  Register #(.width(16)) R0 (.D(register_d_data_i), .en(write_en_bus_s[0]), .clk(clk_i), .Q(R0_q), .clr(rst_i));
  Register #(.width(16)) R1 (.D(register_d_data_i), .en(write_en_bus_s[1]), .clk(clk_i), .Q(R1_q), .clr(rst_i));
  Register #(.width(16)) R2 (.D(register_d_data_i), .en(write_en_bus_s[2]), .clk(clk_i), .Q(R2_q), .clr(rst_i));
  Register #(.width(16)) R3 (.D(register_d_data_i), .en(write_en_bus_s[3]), .clk(clk_i), .Q(R3_q), .clr(rst_i));
  Register #(.width(16)) R4 (.D(register_d_data_i), .en(write_en_bus_s[4]), .clk(clk_i), .Q(R4_q), .clr(rst_i));
  Register #(.width(16)) SP (.D(register_d_data_i), .en(write_en_bus_s[5]), .clk(clk_i), .Q(SP_pres), .clr(rst_i));
  Register #(.width(16)) LR (.D(lr_manager_1_out_9), .en(lr_manager_1_out_10), .clk(clk_i), .Q(LR_pres), .clr(rst_i));
  Register #(.width(16)) PC (.D(multiplexer_1_out), .en(1'b1), .clk(clk_i), .Q(PC_pres_o), .clr(rst_i));
  Multiplexer #(.width(16), .enable("false")) multiplexer_1 (
    .in0(PC_fut_i), .in1(register_d_data_i), .out(multiplexer_1_out), .sel(and_1_out));
  and and_2 (branch_validated_s, bank_reg_en_i, branch_i);
  and and_3 (link_en_validated_s, bank_reg_en_i, link_en_i);
  and and_4 (bank_wr_validated_s, bank_reg_en_i, reg_bank_control_bus_i[1]);
  Register #(.width(16)) register_1 (
    .D(reg_n_read_data_s), .en(1'b1), .clk(clk_i), .Q(register_n_read_data_o), .clr(rst_i));
  Register #(.width(16)) register_2 (
    .D(reg_m_read_data_s), .en(1'b1), .clk(clk_i), .Q(register_m_read_data_o), .clr(rst_i));
  Register #(.width(16)) register_3 (
    .D(reg_mem_read_data_s), .en(1'b1), .clk(clk_i), .Q(register_mem_read_data_o), .clr(rst_i));
  Multiplexer #(.select(3), .width(16), .enable("false")) multiplexer_2 (
    .in0(R0_q), .in1(R1_q), .in2(R2_q), .in3(R3_q), .in4(R4_q), .in5(SP_pres), .in6(LR_pres),
    .in7(PC_pres_o), .out(reg_n_read_data_s), .sel(register_n_sel_i));
  Multiplexer #(.select(3), .width(16), .enable("false")) multiplexer_3 (
    .in0(R0_q), .in1(R1_q), .in2(R2_q), .in3(R3_q), .in4(R4_q), .in5(SP_pres), .in6(LR_pres),
    .in7(PC_pres_o), .out(reg_m_read_data_s), .sel(register_m_sel_i));
  Multiplexer #(.select(3), .width(16), .enable("false")) multiplexer_4 (
    .in0(R0_q), .in1(R1_q), .in2(R2_q), .in3(R3_q), .in4(R4_q), .in5(SP_pres), .in6(LR_pres),
    .in7(PC_pres_o), .out(reg_mem_read_data_s), .sel(register_mem_sel_i));

  // Other names for the same wires on the sheet: bank_en_s = bank_reg_en_i; branch_s = branch_i; clk_s = clk_i;
  //   link_en_s = link_en_i; LR_addr_s[15:0] = LR_addr_i; PC_fut_s[15:0] = PC_fut_i; PC_pres[15:0] = PC_pres_o;
  //   reg_bank_control_bus[1:0] = reg_bank_control_bus_i; bank_wr_s = reg_bank_control_bus_i[1];
  //   reg_d_sel_s[2:0] = register_d_sel_i; reg_m_sel_s[2:0] = register_m_sel_i;
  //   reg_mem_sel_s[2:0] = register_mem_sel_i; reg_n_sel_s[2:0] = register_n_sel_i;
  //   reg_write_data_s[15:0] = register_d_data_i; rst_s = rst_i

  // Notes on the sheet:
  //   Attention, votre version de Logisim
  //   ne contient pas de tracker. Si vous
  //   enregistrez votre projet, toutes les
  //   informations du tracker seront
  //   définitivement effacées.
  //   Sélection du write enable
  //   Split le bus de controle : 
  //   Sélection du bus de sortie registre n
  //   Sélection du bus de sortie registre m
  //   Sélection du bus de sortie registre mem
endmodule

module LR_manager (
  input  [15:0] data_i,
  input  [15:0] pc_fut_lr_i,
  input  [15:0] LR_addr_i,
  input  branch_i,
  input  write_en_i,
  input  link_en_i,
  input  clk_i,
  input  rst_i,
  output [15:0] out_9,
  output out_10
);

  wire and_1_out, d_ff_1_q, link_en_d1_s, or_1_out;
  wire [15:0] multiplexer_1_out;

  D_Flip_Flop d_ff_1 (.D(link_en_i), .clk(clk_i), .Q(d_ff_1_q), .preset(1'b0), .reset(rst_i));  // open: Qn
  D_Flip_Flop d_ff_2 (.D(d_ff_1_q), .clk(clk_i), .Q(link_en_d1_s), .preset(1'b0), .reset(rst_i));  // open: Qn
  D_Flip_Flop d_ff_3 (.D(link_en_d1_s), .clk(clk_i), .preset(1'b0), .reset(rst_i));  // open: Q, Qn
  Multiplexer #(.width(16), .enable("false")) multiplexer_1 (
    .in0(data_i), .in1(pc_fut_lr_i), .out(multiplexer_1_out), .sel(and_1_out));
  and and_1 (and_1_out, branch_i, link_en_i);
  or or_1 (or_1_out, write_en_i, link_en_i);
  Multiplexer #(.width(16), .enable("false")) multiplexer_2 (
    .in0(multiplexer_1_out), .in1(LR_addr_i), .out(out_9), .sel(link_en_d1_s));
  or or_2 (out_10, or_1_out, link_en_d1_s);

  // Other names for the same wires on the sheet: clk_s = clk_i; link_en_s = link_en_i; rst_s = rst_i

  // Notes on the sheet:
  //   Attention, votre version de Logisim
  //   ne contient pas de tracker. Si vous
  //   enregistrez votre projet, toutes les
  //   informations du tracker seront
  //   définitivement effacées.
endmodule

module decode_instr_splitter (
  input  [15:0] instr_i,
  output [2:0] rd_2_0_o,
  output [2:0] rd_10_8_o,
  output [2:0] rn_5_3_o,
  output [2:0] rm_8_6_o,
  output [2:0] offset3_8_6_o,
  output [4:0] offset5_10_6_o,
  output [7:0] offset8_7_0_o,
  output [10:0] offset11_10_0_o,
  output [3:0] cond_11_8_o
);


  assign cond_11_8_o = instr_i[11:8];
  assign offset3_8_6_o = instr_i[8:6];
  assign offset5_10_6_o = instr_i[10:6];
  assign offset8_7_0_o = instr_i[7:0];
  assign offset11_10_0_o = instr_i[10:0];
  assign rd_2_0_o = instr_i[2:0];
  assign rd_10_8_o = instr_i[10:8];
  assign rm_8_6_o = instr_i[8:6];
  assign rn_5_3_o = instr_i[5:3];

  // Notes on the sheet:
  //   Attention, votre version de Logisim
  //   ne contient pas de tracker. Si vous
  //   enregistrez votre projet, toutes les
  //   informations du tracker seront
  //   définitivement effacées.
endmodule

module main_control_unit (
  input  [15:0] instr_i,
  input  [3:0] cond_i,
  input  branch_i,
  input  [2:0] adr_reg_d_i,
  input  [2:0] adr_reg_n_i,
  input  [2:0] adr_reg_m_i,
  input  [2:0] adr_reg_mem_i,
  input  clk_i,
  input  rst_i,
  output [6:0] fetch_control_bus_o,
  output [5:0] decode_control_bus_o,
  output [14:0] execute_control_bus_o,
  output [4:0] mem_control_bus_o,
  output [1:0] reg_bank_control_bus_o,
  output fetch_en_o,
  output decode_en_o,
  output execute_en_o,
  output memory_access_en_o,
  output reg_bank_en_o,
  output [1:0] sel_op1_forward_o,
  output [1:0] sel_op2_forward_o,
  output [1:0] sel_op_mem_forward_o
);

  wire add_r_imm_s, add_r_r_imm_s, add_r_r_r_s, and_r_r_s, asr_r_r_imm_s, asr_r_r_s, b_cond_s, b_incond_s,
       bl_lsb_s, bl_msb_s, byte_s, cond_en_s, eor_r_r_s, instr_control_s, ldr_data_s, ldrb_r_r_imm_s,
       ldrb_r_r_r_s, ldrh_r_r_imm_s, ldrh_r_r_r_s, link_en_s, lsl_r_r_imm_s, lsl_r_r_s, lsr_r_r_imm_s,
       lsr_r_r_s, mov_r_imm_s, mvn_r_r_s, neg_r_r_s, not_1_out, or_1_out, orr_r_r_s, reg_bank_wr_s,
       reg_m_en_s, reg_mem_en_s, reg_n_en_s, ror_r_r_s, sel_cpsr_s, sel_mem_s, sel_operand_1_s, sel_PC_s,
       sel_rd_s, sel_rm_s, sel_shift_s, str_data_s, strb_r_r_imm_s, strb_r_r_r_s, strh_r_r_imm_s,
       strh_r_r_r_s, sub_r_imm_s, sub_r_r_imm_s, sub_r_r_r_s, valid_s;
  wire [1:0] sel_operand_2_s, sel_rn_s;
  wire [2:0] sel_mult_2_s, sel_op_alu_s, sel_op_shift_s;

  opcode_supported_unit opcode_supported_unit_1 (
    .instr_i(instr_i), .lsl_r_r_imm_o(lsl_r_r_imm_s), .lsr_r_r_imm_o(lsr_r_r_imm_s),
    .asr_r_r_imm_o(asr_r_r_imm_s), .add_r_r_r_o(add_r_r_r_s), .add_r_r_imm_o(add_r_r_imm_s),
    .sub_r_r_r_o(sub_r_r_r_s), .sub_r_r_imm_o(sub_r_r_imm_s), .mov_r_imm_o(mov_r_imm_s),
    .add_r_imm_o(add_r_imm_s), .sub_r_imm_o(sub_r_imm_s), .and_r_r_o(and_r_r_s), .eor_r_r_o(eor_r_r_s),
    .lsl_r_r_o(lsl_r_r_s), .lsr_r_r_o(lsr_r_r_s), .asr_r_r_o(asr_r_r_s), .ror_r_r_o(ror_r_r_s),
    .neg_r_r_o(neg_r_r_s), .orr_r_r_o(orr_r_r_s), .mvn_r_r_o(mvn_r_r_s), .strb_r_r_r_o(strb_r_r_r_s),
    .ldrb_r_r_r_o(ldrb_r_r_r_s), .strh_r_r_r_o(strh_r_r_r_s), .ldrh_r_r_r_o(ldrh_r_r_r_s),
    .strb_r_r_imm_o(strb_r_r_imm_s), .ldrb_r_r_imm_o(ldrb_r_r_imm_s), .strh_r_r_imm_o(strh_r_r_imm_s),
    .ldrh_r_r_imm_o(ldrh_r_r_imm_s), .b_cond_o(b_cond_s), .b_incond_o(b_incond_s), .bl_msb_o(bl_msb_s),
    .bl_lsb_o(bl_lsb_s), .valid_o(valid_s));
  fetch_control_unit fetch (
    .instr_i({1'b0, bl_lsb_s, bl_msb_s, b_incond_s, b_cond_s, ldrh_r_r_imm_s, strh_r_r_imm_s, ldrb_r_r_imm_s, strb_r_r_imm_s, ldrh_r_r_r_s, strh_r_r_r_s, ldrb_r_r_r_s, strb_r_r_r_s, mvn_r_r_s, orr_r_r_s, neg_r_r_s, ror_r_r_s, asr_r_r_s, lsr_r_r_s, lsl_r_r_s, eor_r_r_s, and_r_r_s, sub_r_imm_s, add_r_imm_s, mov_r_imm_s, sub_r_r_imm_s, sub_r_r_r_s, add_r_r_imm_s, add_r_r_r_s, asr_r_r_imm_s, lsr_r_r_imm_s, lsl_r_r_imm_s}),
    .sel_cpsr_o(sel_cpsr_s), .link_en_o(link_en_s), .sel_PC_o(sel_PC_s), .cond_en_o(cond_en_s));
  decode_control_unit decode (
    .instr_i({1'b0, bl_lsb_s, bl_msb_s, b_incond_s, b_cond_s, ldrh_r_r_imm_s, strh_r_r_imm_s, ldrb_r_r_imm_s, strb_r_r_imm_s, ldrh_r_r_r_s, strh_r_r_r_s, ldrb_r_r_r_s, strb_r_r_r_s, mvn_r_r_s, orr_r_r_s, neg_r_r_s, ror_r_r_s, asr_r_r_s, lsr_r_r_s, lsl_r_r_s, eor_r_r_s, and_r_r_s, sub_r_imm_s, add_r_imm_s, mov_r_imm_s, sub_r_r_imm_s, sub_r_r_r_s, add_r_r_imm_s, add_r_r_r_s, asr_r_r_imm_s, lsr_r_r_imm_s, lsl_r_r_imm_s}),
    .sel_rn_o(sel_rn_s), .sel_rm_o(sel_rm_s), .sel_rd_o(sel_rd_s));
  reg_bank_control_unit reg_bank (
    .instr_i({1'b0, bl_lsb_s, bl_msb_s, b_incond_s, b_cond_s, ldrh_r_r_imm_s, strh_r_r_imm_s, ldrb_r_r_imm_s, strb_r_r_imm_s, ldrh_r_r_r_s, strh_r_r_r_s, ldrb_r_r_r_s, strb_r_r_r_s, mvn_r_r_s, orr_r_r_s, neg_r_r_s, ror_r_r_s, asr_r_r_s, lsr_r_r_s, lsl_r_r_s, eor_r_r_s, and_r_r_s, sub_r_imm_s, add_r_imm_s, mov_r_imm_s, sub_r_r_imm_s, sub_r_r_r_s, add_r_r_imm_s, add_r_r_r_s, asr_r_r_imm_s, lsr_r_r_imm_s, lsl_r_r_imm_s}),
    .reg_bank_wr_o(reg_bank_wr_s));
  execute_control_unit execute (
    .instr_i({1'b0, bl_lsb_s, bl_msb_s, b_incond_s, b_cond_s, ldrh_r_r_imm_s, strh_r_r_imm_s, ldrb_r_r_imm_s, strb_r_r_imm_s, ldrh_r_r_r_s, strh_r_r_r_s, ldrb_r_r_r_s, strb_r_r_r_s, mvn_r_r_s, orr_r_r_s, neg_r_r_s, ror_r_r_s, asr_r_r_s, lsr_r_r_s, lsl_r_r_s, eor_r_r_s, and_r_r_s, sub_r_imm_s, add_r_imm_s, mov_r_imm_s, sub_r_r_imm_s, sub_r_r_r_s, add_r_r_imm_s, add_r_r_r_s, asr_r_r_imm_s, lsr_r_r_imm_s, lsl_r_r_imm_s}),
    .sel_operand_1_o(sel_operand_1_s), .sel_operand_2_o(sel_operand_2_s), .sel_op_shift_o(sel_op_shift_s),
    .sel_op_alu_o(sel_op_alu_s), .sel_mult_2_o(sel_mult_2_s), .sel_shift_o(sel_shift_s));
  memory_access_control_unit memory_acces (
    .instr_i({1'b0, bl_lsb_s, bl_msb_s, b_incond_s, b_cond_s, ldrh_r_r_imm_s, strh_r_r_imm_s, ldrb_r_r_imm_s, strb_r_r_imm_s, ldrh_r_r_r_s, strh_r_r_r_s, ldrb_r_r_r_s, strb_r_r_r_s, mvn_r_r_s, orr_r_r_s, neg_r_r_s, ror_r_r_s, asr_r_r_s, lsr_r_r_s, lsl_r_r_s, eor_r_r_s, and_r_r_s, sub_r_imm_s, add_r_imm_s, mov_r_imm_s, sub_r_r_imm_s, sub_r_r_r_s, add_r_r_imm_s, add_r_r_r_s, asr_r_r_imm_s, lsr_r_r_imm_s, lsl_r_r_imm_s}),
    .sel_mem_o(sel_mem_s), .str_data_o(str_data_s), .ldr_data_o(ldr_data_s), .byte_o(byte_s));
  bus_constructor bus_constructor_1 (
    .fetch_en_i(1'b0), .decode_en_i(1'b0), .reg_bank_en_i(1'b0), .execute_en_i(1'b0),
    .memory_access_en_i(1'b0), .cond_i(cond_i), .sel_cpsr_i(sel_cpsr_s), .link_en_i(link_en_s),
    .sel_PC_i(sel_PC_s), .cond_en_i(cond_en_s), .sel_rn_i(sel_rn_s), .sel_rm_i(sel_rm_s),
    .sel_rd_i(sel_rd_s), .reg_bank_wr_i(reg_bank_wr_s), .sel_operand_1_i(sel_operand_1_s),
    .sel_operand_2_i(sel_operand_2_s), .sel_op_shift_i(sel_op_shift_s), .sel_op_alu_i(sel_op_alu_s),
    .sel_mult_2_i(sel_mult_2_s), .sel_shift_i(sel_shift_s), .sel_mem_i(sel_mem_s), .str_data_i(str_data_s),
    .ldr_data_i(ldr_data_s), .byte_i(byte_s), .fetch_control_bus_o(fetch_control_bus_o),
    .decode_control_bus_o(decode_control_bus_o), .reg_bank_control_bus_o(reg_bank_control_bus_o),
    .execute_control_bus_o(execute_control_bus_o), .mem_control_bus_o(mem_control_bus_o));
  or or_1 (or_1_out, add_r_r_r_s, sub_r_r_r_s, and_r_r_s, eor_r_r_s, lsl_r_r_s, lsr_r_r_s, asr_r_r_s, ror_r_r_s, orr_r_r_s, strb_r_r_r_s, ldrb_r_r_r_s, strh_r_r_r_s, ldrh_r_r_r_s);
  not not_1 (not_1_out, sel_operand_1_s);
  hazard_detection hazard_detection_1 (
    .instr_control_i(instr_control_s), .reg_bank_write_en_i(reg_bank_wr_s), .adr_reg_d_i(adr_reg_d_i),
    .adr_reg_n_i(adr_reg_n_i), .adr_reg_m_i(adr_reg_m_i), .adr_reg_mem_i(adr_reg_mem_i),
    .reg_n_en_i(reg_n_en_s), .reg_m_en_i(reg_m_en_s), .reg_mem_en_i(reg_mem_en_s), .sel_mem_i(sel_mem_s),
    .branch_i(branch_i), .clk_i(clk_i), .rst_i(rst_i), .fetch_en_o(fetch_en_o), .decode_en_o(decode_en_o),
    .execute_en_o(execute_en_o), .memory_en_o(memory_access_en_o), .bank_register_en(reg_bank_en_o),
    .sel_op2_forward_o(sel_op2_forward_o), .sel_op1_forward_o(sel_op1_forward_o),
    .sel_op_mem_forward_o(sel_op_mem_forward_o));
  or or_2 (instr_control_s, b_cond_s, b_incond_s, bl_lsb_s);
  and and_1 (reg_n_en_s, not_1_out, valid_s);
  and and_2 (reg_m_en_s, or_1_out, valid_s);
  and and_3 (reg_mem_en_s, str_data_s, valid_s);

  // Other names for the same wires on the sheet: adr_reg_d_s[2:0] = adr_reg_d_i; adr_reg_m_s[2:0] = adr_reg_m_i;
  //   adr_reg_mem_s[2:0] = adr_reg_mem_i; adr_reg_n_s[2:0] = adr_reg_n_i; branch_s = branch_i; clk_s = clk_i;
  //   cond_s[3:0] = cond_i; decode_control_bus_s[5:0] = decode_control_bus_o; decode_en_s = decode_en_o;
  //   execute_control_bus_s[14:0] = execute_control_bus_o; execute_en_s = execute_en_o;
  //   fetch_control_bus_s[6:0] = fetch_control_bus_o; fetch_en_s = fetch_en_o;
  //   mem_control_bus_s[4:0] = mem_control_bus_o; memory_access_en_s = memory_access_en_o;
  //   reg_bank_control_bus_s[1:0] = reg_bank_control_bus_o; reg_bank_en_s = reg_bank_en_o; rst_s = rst_i;
  //   sel_op1_forward_s[1:0] = sel_op1_forward_o; sel_op2_forward_s[1:0] = sel_op2_forward_o;
  //   sel_op_mem_forward_s[1:0] = sel_op_mem_forward_o

  // Notes on the sheet:
  //   Attention, votre version de Logisim
  //   ne contient pas de tracker. Si vous
  //   enregistrez votre projet, toutes les
  //   informations du tracker seront
  //   définitivement effacées.
endmodule

module opcode_supported_unit (
  input  [15:0] instr_i,
  output lsl_r_r_imm_o,
  output lsr_r_r_imm_o,
  output asr_r_r_imm_o,
  output add_r_r_r_o,
  output add_r_r_imm_o,
  output sub_r_r_r_o,
  output sub_r_r_imm_o,
  output mov_r_imm_o,
  output add_r_imm_o,
  output sub_r_imm_o,
  output and_r_r_o,
  output eor_r_r_o,
  output lsl_r_r_o,
  output lsr_r_r_o,
  output asr_r_r_o,
  output ror_r_r_o,
  output neg_r_r_o,
  output orr_r_r_o,
  output mvn_r_r_o,
  output strb_r_r_r_o,
  output ldrb_r_r_r_o,
  output strh_r_r_r_o,
  output ldrh_r_r_r_o,
  output strb_r_r_imm_o,
  output ldrb_r_r_imm_o,
  output strh_r_r_imm_o,
  output ldrh_r_r_imm_o,
  output b_cond_o,
  output b_incond_o,
  output bl_msb_o,
  output bl_lsb_o,
  output valid_o
);

  wire comparator_28_eq, comparator_29_eq;

  Comparator #(.width(5), .mode("unsigned")) comparator_1 (
    .a(instr_i[15:11]), .b({5{1'b0}}), .eq(lsl_r_r_imm_o));  // open: gt, lt
  Comparator #(.width(5), .mode("unsigned")) comparator_2 (
    .a(instr_i[15:11]), .b(5'b00001), .eq(lsr_r_r_imm_o));  // open: gt, lt
  Comparator #(.width(5), .mode("unsigned")) comparator_3 (
    .a(instr_i[15:11]), .b(5'b00010), .eq(asr_r_r_imm_o));  // open: gt, lt
  Comparator #(.width(7), .mode("unsigned")) comparator_4 (
    .a(instr_i[15:9]), .b(7'b0001100), .eq(add_r_r_r_o));  // open: gt, lt
  Comparator #(.width(7), .mode("unsigned")) comparator_5 (
    .a(instr_i[15:9]), .b(7'b0001110), .eq(add_r_r_imm_o));  // open: gt, lt
  Comparator #(.width(7), .mode("unsigned")) comparator_6 (
    .a(instr_i[15:9]), .b(7'b0001101), .eq(sub_r_r_r_o));  // open: gt, lt
  Comparator #(.width(7), .mode("unsigned")) comparator_7 (
    .a(instr_i[15:9]), .b(7'b0001111), .eq(sub_r_r_imm_o));  // open: gt, lt
  Comparator #(.width(5), .mode("unsigned")) comparator_8 (
    .a(instr_i[15:11]), .b(5'b00100), .eq(mov_r_imm_o));  // open: gt, lt
  Comparator #(.width(5), .mode("unsigned")) comparator_9 (
    .a(instr_i[15:11]), .b(5'b00110), .eq(add_r_imm_o));  // open: gt, lt
  Comparator #(.width(5), .mode("unsigned")) comparator_10 (
    .a(instr_i[15:11]), .b(5'b00111), .eq(sub_r_imm_o));  // open: gt, lt
  Comparator #(.width(10), .mode("unsigned")) comparator_11 (
    .a(instr_i[15:6]), .b(10'h100), .eq(and_r_r_o));  // open: gt, lt
  Comparator #(.width(10), .mode("unsigned")) comparator_12 (
    .a(instr_i[15:6]), .b(10'h101), .eq(eor_r_r_o));  // open: gt, lt
  Comparator #(.width(10), .mode("unsigned")) comparator_13 (
    .a(instr_i[15:6]), .b(10'h102), .eq(lsl_r_r_o));  // open: gt, lt
  Comparator #(.width(10), .mode("unsigned")) comparator_14 (
    .a(instr_i[15:6]), .b(10'h103), .eq(lsr_r_r_o));  // open: gt, lt
  Comparator #(.width(10), .mode("unsigned")) comparator_15 (
    .a(instr_i[15:6]), .b(10'h104), .eq(asr_r_r_o));  // open: gt, lt
  Comparator #(.width(10), .mode("unsigned")) comparator_16 (
    .a(instr_i[15:6]), .b(10'h107), .eq(ror_r_r_o));  // open: gt, lt
  Comparator #(.width(10), .mode("unsigned")) comparator_17 (
    .a(instr_i[15:6]), .b(10'h109), .eq(neg_r_r_o));  // open: gt, lt
  Comparator #(.width(10), .mode("unsigned")) comparator_18 (
    .a(instr_i[15:6]), .b(10'h10c), .eq(orr_r_r_o));  // open: gt, lt
  Comparator #(.width(10), .mode("unsigned")) comparator_19 (
    .a(instr_i[15:6]), .b(10'h10f), .eq(mvn_r_r_o));  // open: gt, lt
  Comparator #(.width(7), .mode("unsigned")) comparator_20 (
    .a(instr_i[15:9]), .b(7'b0101010), .eq(strb_r_r_r_o));  // open: gt, lt
  Comparator #(.width(7), .mode("unsigned")) comparator_21 (
    .a(instr_i[15:9]), .b(7'b0101110), .eq(ldrb_r_r_r_o));  // open: gt, lt
  Comparator #(.width(7), .mode("unsigned")) comparator_22 (
    .a(instr_i[15:9]), .b(7'b0101001), .eq(strh_r_r_r_o));  // open: gt, lt
  Comparator #(.width(7), .mode("unsigned")) comparator_23 (
    .a(instr_i[15:9]), .b(7'b0101101), .eq(ldrh_r_r_r_o));  // open: gt, lt
  Comparator #(.width(5), .mode("unsigned")) comparator_24 (
    .a(instr_i[15:11]), .b(5'b01110), .eq(strb_r_r_imm_o));  // open: gt, lt
  Comparator #(.width(5), .mode("unsigned")) comparator_25 (
    .a(instr_i[15:11]), .b(5'b01111), .eq(ldrb_r_r_imm_o));  // open: gt, lt
  Comparator #(.width(5), .mode("unsigned")) comparator_26 (
    .a(instr_i[15:11]), .b(5'b10000), .eq(strh_r_r_imm_o));  // open: gt, lt
  Comparator #(.width(5), .mode("unsigned")) comparator_27 (
    .a(instr_i[15:11]), .b(5'b10001), .eq(ldrh_r_r_imm_o));  // open: gt, lt
  Comparator #(.width(4), .mode("unsigned")) comparator_28 (
    .a(instr_i[15:12]), .b(4'b1101), .eq(comparator_28_eq));  // open: gt, lt
  Comparator #(.width(4), .mode("unsigned")) comparator_29 (
    .a(instr_i[11:8]), .b(4'b1111), .eq(comparator_29_eq));  // open: gt, lt
  Comparator #(.width(5), .mode("unsigned")) comparator_30 (
    .a(instr_i[15:11]), .b(5'b11100), .eq(b_incond_o));  // open: gt, lt
  Comparator #(.width(5), .mode("unsigned")) comparator_31 (
    .a(instr_i[15:11]), .b(5'b11110), .eq(bl_msb_o));  // open: gt, lt
  Comparator #(.width(5), .mode("unsigned")) comparator_32 (
    .a(instr_i[15:11]), .b({5{1'b1}}), .eq(bl_lsb_o));  // open: gt, lt
  and and_1 (b_cond_o, comparator_28_eq, ~comparator_29_eq);  // AND_Gate
  or or_1 (valid_o, lsl_r_r_imm_o, lsr_r_r_imm_o, asr_r_r_imm_o, add_r_r_r_o, add_r_r_imm_o, sub_r_r_r_o, sub_r_r_imm_o, mov_r_imm_o, add_r_imm_o, sub_r_imm_o, and_r_r_o, eor_r_r_o, lsl_r_r_o, lsr_r_r_o, asr_r_r_o, ror_r_r_o, neg_r_r_o, orr_r_r_o, mvn_r_r_o, strb_r_r_r_o, ldrb_r_r_r_o, strh_r_r_r_o, ldrh_r_r_r_o, strb_r_r_imm_o, ldrb_r_r_imm_o, strh_r_r_imm_o, ldrh_r_r_imm_o, b_cond_o, b_incond_o, bl_msb_o, bl_lsb_o);

  // Other names for the same wires on the sheet: add_r_imm = add_r_imm_o; add_r_r_imm = add_r_r_imm_o;
  //   add_r_r_r = add_r_r_r_o; and_r_r = and_r_r_o; asr_r_r = asr_r_r_o; asr_r_r_imm = asr_r_r_imm_o;
  //   b_cond = b_cond_o; b_incond = b_incond_o; bl_lsb = bl_lsb_o; bl_msb = bl_msb_o; eor_r_r = eor_r_r_o;
  //   ldrb_r_r_imm = ldrb_r_r_imm_o; ldrb_r_r_r = ldrb_r_r_r_o; ldrh_r_r_imm = ldrh_r_r_imm_o;
  //   ldrh_r_r_r = ldrh_r_r_r_o; lsl_r_r = lsl_r_r_o; lsl_r_r_imm = lsl_r_r_imm_o; lsr_r_r = lsr_r_r_o;
  //   lsr_r_r_imm = lsr_r_r_imm_o; mov_r_imm = mov_r_imm_o; mvn_r_r = mvn_r_r_o; neg_r_r = neg_r_r_o;
  //   orr_r_r = orr_r_r_o; ror_r_r = ror_r_r_o; strb_r_r_imm = strb_r_r_imm_o; strb_r_r_r = strb_r_r_r_o;
  //   strh_r_r_imm = strh_r_r_imm_o; strh_r_r_r = strh_r_r_r_o; sub_r_imm = sub_r_imm_o; sub_r_r_imm = sub_r_r_imm_o;
  //   sub_r_r_r = sub_r_r_r_o

  // Notes on the sheet:
  //   Attention, votre version de Logisim
  //   ne contient pas de tracker. Si vous
  //   enregistrez votre projet, toutes les
  //   informations du tracker seront
  //   définitivement effacées.
  //   Extraction des instructions supportées
endmodule

module fetch_control_unit (
  input  [31:0] instr_i,
  output sel_cpsr_o,
  output link_en_o,
  output sel_PC_o,
  output cond_en_o
);

  or or_1 (sel_PC_o, instr_i[27], instr_i[28], instr_i[30]);
  or or_2 (sel_cpsr_o, instr_i[0], instr_i[1], instr_i[2], instr_i[3], instr_i[4], instr_i[5], instr_i[6], instr_i[7], instr_i[8], instr_i[9], instr_i[10], instr_i[11], instr_i[12], instr_i[13], instr_i[14], instr_i[15], instr_i[16], instr_i[17], instr_i[18]);

  assign cond_en_o = instr_i[27];
  assign link_en_o = instr_i[29];

  // Other names for the same wires on the sheet: lsl_r_r_imm_s = instr_i[0]; lsr_r_r_imm_s = instr_i[1];
  //   asr_r_r_imm_s = instr_i[2]; add_r_r_r_s = instr_i[3]; add_r_r_imm_s = instr_i[4]; sub_r_r_r_s = instr_i[5];
  //   sub_r_r_imm_s = instr_i[6]; mov_r_imm_s = instr_i[7]; add_r_imm_s = instr_i[8]; sub_r_imm_s = instr_i[9];
  //   and_r_r_s = instr_i[10]; eor_r_r_s = instr_i[11]; lsl_r_r_s = instr_i[12]; lsr_r_r_s = instr_i[13];
  //   asr_r_r_s = instr_i[14]; ror_r_r_s = instr_i[15]; neg_r_r_s = instr_i[16]; orr_r_r_s = instr_i[17];
  //   mvn_r_r_s = instr_i[18]; strb_r_r_r_s = instr_i[19]; ldrb_r_r_r_s = instr_i[20]; strh_r_r_r_s = instr_i[21];
  //   ldrh_r_r_r_s = instr_i[22]; strb_r_r_imm_s = instr_i[23]; ldrb_r_r_imm_s = instr_i[24];
  //   strh_r_r_imm_s = instr_i[25]; ldrh_r_r_imm_s = instr_i[26]; b_cond_s = instr_i[27]; cond_en_s = instr_i[27];
  //   b_incond_s = instr_i[28]; bl_msb_s = instr_i[29]; link_en_s = instr_i[29]; bl_lsb_s = instr_i[30];
  //   sel_cpsr_s = sel_cpsr_o; sel_PC_s = sel_PC_o

  // Notes on the sheet:
  //   Attention, votre version de Logisim
  //   ne contient pas de tracker. Si vous
  //   enregistrez votre projet, toutes les
  //   informations du tracker seront
  //   définitivement effacées.
endmodule

module decode_control_unit (
  input  [31:0] instr_i,
  output [1:0] sel_rn_o,
  output sel_rm_o,
  output sel_rd_o
);

  or or_1 (sel_rn_o[1], instr_i[30], instr_i[29], instr_i[27], instr_i[28]);
  or or_2 (sel_rd_o, instr_i[7], instr_i[8], instr_i[9]);
  or or_3 (sel_rn_o[0], instr_i[8], instr_i[10], instr_i[11], instr_i[12], instr_i[13], instr_i[30], instr_i[14], instr_i[15], instr_i[17], 1'b0, instr_i[9]);
  or or_4 (sel_rm_o, instr_i[12], instr_i[17], instr_i[11], instr_i[13], instr_i[15], instr_i[14], instr_i[10]);

  // Other names for the same wires on the sheet: lsl_r_r_imm_s = instr_i[0]; lsr_r_r_imm_s = instr_i[1];
  //   asr_r_r_imm_s = instr_i[2]; add_r_r_r_s = instr_i[3]; add_r_r_imm_s = instr_i[4]; sub_r_r_r_s = instr_i[5];
  //   sub_r_r_imm_s = instr_i[6]; mov_r_imm_s = instr_i[7]; add_r_imm_s = instr_i[8]; sub_r_imm_s = instr_i[9];
  //   and_r_r_s = instr_i[10]; eor_r_r_s = instr_i[11]; lsl_r_r_s = instr_i[12]; lsr_r_r_s = instr_i[13];
  //   asr_r_r_s = instr_i[14]; ror_r_r_s = instr_i[15]; neg_r_r_s = instr_i[16]; orr_r_r_s = instr_i[17];
  //   mvn_r_r_s = instr_i[18]; strb_r_r_r_s = instr_i[19]; ldrb_r_r_r_s = instr_i[20]; strh_r_r_r_s = instr_i[21];
  //   ldrh_r_r_r_s = instr_i[22]; strb_r_r_imm_s = instr_i[23]; ldrb_r_r_imm_s = instr_i[24];
  //   strh_r_r_imm_s = instr_i[25]; ldrh_r_r_imm_s = instr_i[26]; b_cond_s = instr_i[27]; b_incond_s = instr_i[28];
  //   bl_msb_s = instr_i[29]; bl_lsb_s = instr_i[30]; sel_rd_s = sel_rd_o; sel_rm_s = sel_rm_o;
  //   sel_rn_s[1:0] = sel_rn_o

  // Notes on the sheet:
  //   Attention, votre version de Logisim
  //   ne contient pas de tracker. Si vous
  //   enregistrez votre projet, toutes les
  //   informations du tracker seront
  //   définitivement effacées.
endmodule

module reg_bank_control_unit (
  input  [31:0] instr_i,
  output reg_bank_wr_o
);

  or or_1 (reg_bank_wr_o, instr_i[0], instr_i[1], instr_i[2], instr_i[3], instr_i[4], instr_i[5], instr_i[6], instr_i[7], instr_i[8], instr_i[9], instr_i[10], instr_i[11], instr_i[12], instr_i[13], instr_i[14], instr_i[15], instr_i[16], instr_i[17], instr_i[18], instr_i[20], instr_i[22], instr_i[24], instr_i[26], 1'b0, instr_i[29], instr_i[30]);

  // Other names for the same wires on the sheet: lsl_r_r_imm_s = instr_i[0]; lsr_r_r_imm_s = instr_i[1];
  //   asr_r_r_imm_s = instr_i[2]; add_r_r_r_s = instr_i[3]; add_r_r_imm_s = instr_i[4]; sub_r_r_r_s = instr_i[5];
  //   sub_r_r_imm_s = instr_i[6]; mov_r_imm_s = instr_i[7]; add_r_imm_s = instr_i[8]; sub_r_imm_s = instr_i[9];
  //   and_r_r_s = instr_i[10]; eor_r_r_s = instr_i[11]; lsl_r_r_s = instr_i[12]; lsr_r_r_s = instr_i[13];
  //   asr_r_r_s = instr_i[14]; ror_r_r_s = instr_i[15]; neg_r_r_s = instr_i[16]; orr_r_r_s = instr_i[17];
  //   mvn_r_r_s = instr_i[18]; strb_r_r_r_s = instr_i[19]; ldrb_r_r_r_s = instr_i[20]; strh_r_r_r_s = instr_i[21];
  //   ldrh_r_r_r_s = instr_i[22]; strb_r_r_imm_s = instr_i[23]; ldrb_r_r_imm_s = instr_i[24];
  //   strh_r_r_imm_s = instr_i[25]; ldrh_r_r_imm_s = instr_i[26]; b_cond_s = instr_i[27]; b_incond_s = instr_i[28];
  //   bl_msb_s = instr_i[29]; bl_lsb_s = instr_i[30]; reg_bank_wr_s = reg_bank_wr_o

  // Notes on the sheet:
  //   Attention, votre version de Logisim
  //   ne contient pas de tracker. Si vous
  //   enregistrez votre projet, toutes les
  //   informations du tracker seront
  //   définitivement effacées.
endmodule

module execute_control_unit (
  input  [31:0] instr_i,
  output sel_operand_1_o,
  output [1:0] sel_operand_2_o,
  output [2:0] sel_op_shift_o,
  output [2:0] sel_op_alu_o,
  output [2:0] sel_mult_2_o,
  output sel_shift_o
);

  or or_1 (sel_op_alu_o[1], instr_i[5], instr_i[6], instr_i[9], instr_i[10], instr_i[11], instr_i[16]);
  or or_2 (sel_op_alu_o[2], instr_i[11], instr_i[16], instr_i[17], instr_i[18]);
  or or_3 (sel_op_alu_o[0], instr_i[27], instr_i[28], instr_i[29], instr_i[30], instr_i[3], instr_i[4], instr_i[7], instr_i[8], instr_i[10], instr_i[11], instr_i[18], instr_i[19], instr_i[20], instr_i[21], instr_i[22], instr_i[23], instr_i[24], instr_i[25], instr_i[26]);
  or or_4 (sel_operand_2_o[0], instr_i[4], instr_i[6], instr_i[7], instr_i[8], instr_i[9]);
  or or_5 (sel_operand_2_o[1], instr_i[7], instr_i[8], instr_i[9], instr_i[23], instr_i[24], instr_i[25], instr_i[26], instr_i[27], instr_i[28], instr_i[29], instr_i[30]);
  or or_6 (sel_mult_2_o[0], instr_i[29], instr_i[28], instr_i[30]);
  or or_7 (sel_mult_2_o[1], instr_i[30], instr_i[27]);
  or or_8 (sel_mult_2_o[2], instr_i[19], instr_i[23], instr_i[20], instr_i[24], instr_i[29]);
  or or_9 (sel_op_shift_o[0], instr_i[1], instr_i[13], instr_i[2], instr_i[14]);
  or or_10 (sel_op_shift_o[1], instr_i[0], instr_i[1], instr_i[12], instr_i[13]);
  or or_11 (sel_shift_o, instr_i[12], instr_i[13], instr_i[14], instr_i[15]);

  assign sel_op_shift_o[2] = instr_i[15];
  assign sel_operand_1_o = instr_i[7];

  // Other names for the same wires on the sheet: lsl_r_r_imm_s = instr_i[0]; lsr_r_r_imm_s = instr_i[1];
  //   asr_r_r_imm_s = instr_i[2]; add_r_r_r_s = instr_i[3]; add_r_r_imm_s = instr_i[4]; sub_r_r_r_s = instr_i[5];
  //   sub_r_r_imm_s = instr_i[6]; mov_r_imm_s = instr_i[7]; sel_operand_1_s = instr_i[7]; add_r_imm_s = instr_i[8];
  //   sub_r_imm_s = instr_i[9]; and_r_r_s = instr_i[10]; eor_r_r_s = instr_i[11]; lsl_r_r_s = instr_i[12];
  //   lsr_r_r_s = instr_i[13]; asr_r_r_s = instr_i[14]; neg_r_r_s = instr_i[16]; orr_r_r_s = instr_i[17];
  //   mvn_r_r_s = instr_i[18]; strb_r_r_r_s = instr_i[19]; ldrb_r_r_r_s = instr_i[20]; strh_r_r_r_s = instr_i[21];
  //   ldrh_r_r_r_s = instr_i[22]; strb_r_r_imm_s = instr_i[23]; ldrb_r_r_imm_s = instr_i[24];
  //   strh_r_r_imm_s = instr_i[25]; ldrh_r_r_imm_s = instr_i[26]; b_cond_s = instr_i[27]; b_incond_s = instr_i[28];
  //   bl_msb_s = instr_i[29]; bl_lsb_s = instr_i[30]; sel_mult_2_s[2:0] = sel_mult_2_o;
  //   sel_op_alu_0_s = sel_op_alu_o[0]; sel_op_alu_s[2:0] = sel_op_alu_o; sel_op_alu_1_s = sel_op_alu_o[1];
  //   sel_op_alu_2_s = sel_op_alu_o[2]; sel_op_shift_0_s = sel_op_shift_o[0];
  //   sel_op_shift_s[2:0] = {instr_i[15], sel_op_shift_o[1:0]}; sel_op_shift_1_s = sel_op_shift_o[1];
  //   ror_r_r_s = instr_i[15]; sel_op_shift_2_s = instr_i[15]; sel_operand_2_s[1:0] = sel_operand_2_o;
  //   sel_shift_s = sel_shift_o

  // Notes on the sheet:
  //   Attention, votre version de Logisim
  //   ne contient pas de tracker. Si vous
  //   enregistrez votre projet, toutes les
  //   informations du tracker seront
  //   définitivement effacées.
endmodule

module memory_access_control_unit (
  input  [31:0] instr_i,
  output sel_mem_o,
  output str_data_o,
  output ldr_data_o,
  output byte_o
);

  or or_1 (sel_mem_o, instr_i[19], instr_i[20], instr_i[21], instr_i[22], instr_i[23], instr_i[24], instr_i[25], instr_i[26]);
  or or_2 (str_data_o, instr_i[19], instr_i[21], instr_i[23], instr_i[25]);
  or or_3 (ldr_data_o, instr_i[20], instr_i[22], instr_i[24], instr_i[26]);
  or or_4 (byte_o, instr_i[19], instr_i[23], instr_i[20], instr_i[24]);

  // Other names for the same wires on the sheet: byte_s = byte_o; lsl_r_r_imm_s = instr_i[0];
  //   lsr_r_r_imm_s = instr_i[1]; asr_r_r_imm_s = instr_i[2]; add_r_r_r_s = instr_i[3]; add_r_r_imm_s = instr_i[4];
  //   sub_r_r_r_s = instr_i[5]; sub_r_r_imm_s = instr_i[6]; mov_r_imm_s = instr_i[7]; add_r_imm_s = instr_i[8];
  //   sub_r_imm_s = instr_i[9]; and_r_r_s = instr_i[10]; eor_r_r_s = instr_i[11]; lsl_r_r_s = instr_i[12];
  //   lsr_r_r_s = instr_i[13]; asr_r_r_s = instr_i[14]; ror_r_r_s = instr_i[15]; neg_r_r_s = instr_i[16];
  //   orr_r_r_s = instr_i[17]; mvn_r_r_s = instr_i[18]; strb_r_r_r_s = instr_i[19]; ldrb_r_r_r_s = instr_i[20];
  //   strh_r_r_r_s = instr_i[21]; ldrh_r_r_r_s = instr_i[22]; strb_r_r_imm_s = instr_i[23];
  //   ldrb_r_r_imm_s = instr_i[24]; strh_r_r_imm_s = instr_i[25]; ldrh_r_r_imm_s = instr_i[26];
  //   b_cond_s = instr_i[27]; b_incond_s = instr_i[28]; bl_msb_s = instr_i[29]; bl_lsb_s = instr_i[30];
  //   ldr_data_s = ldr_data_o; sel_mem_s = sel_mem_o; str_data_s = str_data_o

  // Notes on the sheet:
  //   Attention, votre version de Logisim
  //   ne contient pas de tracker. Si vous
  //   enregistrez votre projet, toutes les
  //   informations du tracker seront
  //   définitivement effacées.
endmodule

module bus_constructor (
  input  fetch_en_i,
  input  decode_en_i,
  input  reg_bank_en_i,
  input  execute_en_i,
  input  memory_access_en_i,
  input  [3:0] cond_i,
  input  sel_cpsr_i,
  input  link_en_i,
  input  sel_PC_i,
  input  cond_en_i,
  input  [1:0] sel_rn_i,
  input  sel_rm_i,
  input  sel_rd_i,
  input  reg_bank_wr_i,
  input  sel_operand_1_i,
  input  [1:0] sel_operand_2_i,
  input  [2:0] sel_op_shift_i,
  input  [2:0] sel_op_alu_i,
  input  [2:0] sel_mult_2_i,
  input  sel_shift_i,
  input  sel_mem_i,
  input  str_data_i,
  input  ldr_data_i,
  input  byte_i,
  output [6:0] fetch_control_bus_o,
  output [5:0] decode_control_bus_o,
  output [1:0] reg_bank_control_bus_o,
  output [14:0] execute_control_bus_o,
  output [4:0] mem_control_bus_o
);


  assign decode_control_bus_o = {1'b0, sel_rd_i, link_en_i, sel_rm_i, sel_rn_i};
  assign execute_control_bus_o = {1'b0, sel_mult_2_i, sel_cpsr_i, sel_shift_i, sel_operand_1_i, sel_operand_2_i, sel_op_alu_i, sel_op_shift_i};
  assign fetch_control_bus_o = {1'b0, cond_i, cond_en_i, sel_PC_i};
  assign mem_control_bus_o = {1'b0, byte_i, ldr_data_i, str_data_i, sel_mem_i};
  assign reg_bank_control_bus_o = {reg_bank_wr_i, 1'b0};

  // Other names for the same wires on the sheet: decode_control_bus_s[4:0] = {sel_rd_i, link_en_i, sel_rm_i, sel_rn_i};
  //   sel_rn_s[1:0] = sel_rn_i; sel_rm_s = sel_rm_i; link_en_s = link_en_i; sel_rd_s = sel_rd_i;
  //   decode_en_s = decode_en_i;
  //   execute_control_bus_s[13:0] = {sel_mult_2_i, sel_cpsr_i, sel_shift_i, sel_operand_1_i, sel_operand_2_i, sel_op_alu_i, sel_op_shift_i};
  //   sel_op_shift_s[2:0] = sel_op_shift_i; sel_op_alu_s[2:0] = sel_op_alu_i; sel_operand_2_s[1:0] = sel_operand_2_i;
  //   sel_operand_1_s = sel_operand_1_i; sel_shift_s = sel_shift_i; sel_cpsr_s = sel_cpsr_i;
  //   sel_mult_2_s[2:0] = sel_mult_2_i; execute_en_s = execute_en_i;
  //   fetch_control_bus_s[5:0] = {cond_i, cond_en_i, sel_PC_i}; sel_PC_s = sel_PC_i; cond_en_s = cond_en_i;
  //   cond_s[3:0] = cond_i; fetch_en_s = fetch_en_i;
  //   mem_control_bus_s[3:0] = {byte_i, ldr_data_i, str_data_i, sel_mem_i}; sel_mem_s = sel_mem_i;
  //   str_data_s = str_data_i; ldr_data_s = ldr_data_i; byte_s = byte_i; memory_access_en_s = memory_access_en_i;
  //   reg_bank_control_bus_s[1] = reg_bank_wr_i; reg_bank_wr_s = reg_bank_wr_i; reg_bank_en_s = reg_bank_en_i

  // Notes on the sheet:
  //   Attention, votre version de Logisim
  //   ne contient pas de tracker. Si vous
  //   enregistrez votre projet, toutes les
  //   informations du tracker seront
  //   définitivement effacées.
endmodule

module execute (
  input  [15:0] reg_data_n_i,
  input  [15:0] reg_data_m_i,
  input  [15:0] reg_mem_read_data_i,
  input  [2:0] addr_reg_d_i,
  input  [2:0] imm3,
  input  [4:0] imm5,
  input  [10:0] offset_incond,
  input  [7:0] offset_cond,
  input  [7:0] imm8,
  input  [15:0] lr_addr_i,
  input  [6:0] fetch_ctl_bus_i,
  input  [14:0] execute_control_bus,
  input  [4:0] mem_ctl_bus_i,
  input  [1:0] reg_bank_ctl_bus_i,
  input  link_en_i,
  input  [1:0] sel_op1_forward_i,
  input  [1:0] sel_op2_forward_i,
  input  [1:0] sel_op_mem_forward_i,
  input  execute_en_i,
  input  [15:0] memory_data_out_i,
  input  [15:0] execute_data_out_i,
  input  clk_i,
  input  rst_i,
  output [15:0] data_o,
  output [3:0] cpsr_o,
  output [2:0] addr_reg_d_o,
  output [6:0] fetch_ctl_bus_o,
  output [4:0] mem_ctl_bus_o,
  output [1:0] reg_bank_ctl_bus_o,
  output [15:0] lr_addr_o,
  output link_en_o,
  output [15:0] reg_mem_read_data_o,
  output execute_en_o,
  output branch_o
);

  wire alu_1_carry_o, alu_1_overflow_o, and_1_out, and_2_out, condition_tester_1_cond_test_o;
  wire [3:0] sel_shift_data_s, zcnv_unit_1_z_o;
  wire [15:0] bit_extender_1_out, mult_2_1_mult_2_out, multiplexer_1_out, multiplexer_2_out,
       shift_1_shift_data_out_o, write_back_data_out_s;

  Register #(.width(16)) register_1 (
    .D(memory_data_out_i), .en(1'b1), .clk(clk_i), .Q(write_back_data_out_s));  // open: clr
  mult_2 mult_2_1 (
    .imm5_i(imm5), .offset_incond_i(offset_incond), .offset_cond_i(offset_cond),
    .sel_mult_2_i(execute_control_bus[13:11]), .mult_2_out(mult_2_1_mult_2_out));
  assign bit_extender_1_out = {{8{1'b0}}, imm8};  // Bit_Extender bit_extender_1
  Multiplexer #(.width(16), .enable("false")) multiplexer_1 (
    .in0(reg_data_n_i), .in1({16{1'b0}}), .out(multiplexer_1_out), .sel(execute_control_bus[8]));
  Multiplexer #(.select(2), .width(16), .enable("false")) multiplexer_2 (
    .in0(reg_data_m_i), .in1({{13{1'b0}}, imm3}), .in2(mult_2_1_mult_2_out), .in3(bit_extender_1_out),
    .out(multiplexer_2_out), .sel(execute_control_bus[7:6]));
  Multiplexer #(.width(4), .enable("false")) multiplexer_3 (
    .in0(imm5[3:0]), .in1(reg_data_m_i[3:0]), .out(sel_shift_data_s), .sel(execute_control_bus[9]));
  shift shift_1 (
    .operand_i(multiplexer_1_out), .sel_shift_data_i(sel_shift_data_s),
    .sel_op_shift_i(execute_control_bus[2:0]), .shift_data_out_o(shift_1_shift_data_out_o));
  zcnv_unit zcnv_unit_1 (
    .data_i(data_o), .carry_i(alu_1_carry_o), .overflow_i(alu_1_overflow_o), .z_o(zcnv_unit_1_z_o[0]),
    .c_o(zcnv_unit_1_z_o[1]), .n_o(zcnv_unit_1_z_o[2]), .v_o(zcnv_unit_1_z_o[3]));
  alu alu_1 (
    .operand_1_i(shift_1_shift_data_out_o), .operand_2_i(multiplexer_2_out),
    .sel_op_alu_i(execute_control_bus[5:3]), .alu_data_out_o(data_o), .carry_o(alu_1_carry_o),
    .overflow_o(alu_1_overflow_o));
  and and_1 (and_1_out, execute_en_i, execute_control_bus[10]);
  condition_tester condition_tester_1 (
    .cond_en_i(fetch_ctl_bus_i[1]), .cond_i(fetch_ctl_bus_i[5:2]), .Z_i(cpsr_o[0]), .C_i(cpsr_o[1]),
    .N_i(cpsr_o[2]), .V_i(cpsr_o[3]), .cond_test_o(condition_tester_1_cond_test_o));
  Register #(.width(4)) CPSR (.D(zcnv_unit_1_z_o), .en(and_1_out), .clk(clk_i), .Q(cpsr_o), .clr(rst_i));
  and and_2 (and_2_out, fetch_ctl_bus_i[0], condition_tester_1_cond_test_o);
  Multiplexer #(.select(2), .width(16), .enable("false")) multiplexer_4 (
    .in0(reg_mem_read_data_i), .in1(execute_data_out_i), .in2(memory_data_out_i),
    .in3(write_back_data_out_s), .out(reg_mem_read_data_o), .sel(sel_op_mem_forward_i));
  Multiplexer #(.enable("false")) multiplexer_5 (.in0(1'b0), .in1(and_2_out), .out(branch_o), .sel(execute_en_i));

  assign addr_reg_d_o = addr_reg_d_i;
  assign execute_en_o = execute_en_i;
  assign fetch_ctl_bus_o = fetch_ctl_bus_i;
  assign link_en_o = link_en_i;
  assign lr_addr_o = lr_addr_i;
  assign mem_ctl_bus_o = mem_ctl_bus_i;
  assign reg_bank_ctl_bus_o = reg_bank_ctl_bus_i;

  // Other names for the same wires on the sheet: imm3_s[2:0] = imm3; adr_reg_d_s[2:0] = addr_reg_d_i; clk_s = clk_i;
  //   sel_op_shift_s[2:0] = execute_control_bus[2:0]; sel_op_alu_s[2:0] = execute_control_bus[5:3];
  //   sel_operand_2_s[1:0] = execute_control_bus[7:6]; sel_operand_1_s = execute_control_bus[8];
  //   sel_shift_s = execute_control_bus[9]; sel_cpsr_s = execute_control_bus[10];
  //   sel_mult_s[2:0] = execute_control_bus[13:11]; execute_data_out_s[15:0] = execute_data_out_i;
  //   execute_en_s = execute_en_i; fetch_control_bus_s[6:0] = fetch_ctl_bus_i; imm5_s[4:0] = imm5; imm8_s[7:0] = imm8;
  //   link_en_s = link_en_i; LR_adr_s[15:0] = lr_addr_i; mem_control_bus_s[4:0] = mem_ctl_bus_i;
  //   memory_data_out_s[15:0] = memory_data_out_i; offset_cond_s[7:0] = offset_cond;
  //   offset_incond_s[10:0] = offset_incond; reg_bank_control_bus_s[1:0] = reg_bank_ctl_bus_i;
  //   reg_data_m_s[15:0] = reg_data_m_i; reg_data_n_s[15:0] = reg_data_n_i;
  //   reg_mem_read_data_s[15:0] = reg_mem_read_data_i; rst_s = rst_i; sel_op1_forward_s[1:0] = sel_op1_forward_i;
  //   sel_op2_forward_s[1:0] = sel_op2_forward_i; sel_op_mem_forward_s[1:0] = sel_op_mem_forward_i

  // Notes on the sheet:
  //   Attention, votre version de Logisim
  //   ne contient pas de tracker. Si vous
  //   enregistrez votre projet, toutes les
  //   informations du tracker seront
  //   définitivement effacées.
  //   Entité EXECUTE
  //   Sel Operand 1
  //   Sel Operand 2
  //   Sel Shift
  //   sel_PC
  //   cond_en_s
  //   cond_s
  //   cond_test_s
  //   branch_s
endmodule

module execute_memory_reg (
  input  [15:0] data_i,
  input  [3:0] cpsr_i,
  input  [2:0] adr_reg_d_i,
  input  [6:0] fetch_ctl_bus_i,
  input  [4:0] mem_ctl_bus_i,
  input  [1:0] reg_bank_ctl_bus_i,
  input  [15:0] lr_addr_i,
  input  link_en_i,
  input  [15:0] reg_mem_read_data_i,
  input  execute_en_i,
  input  branch_i,
  input  clk_i,
  input  rst_i,
  output [15:0] data_o,
  output [3:0] cpsr_o,
  output [2:0] adr_reg_d_o,
  output [6:0] fetch_ctl_bus_o,
  output [4:0] mem_ctl_bus_o,
  output [1:0] reg_bank_ctl_bus_o,
  output [15:0] lr_addr_o,
  output link_en_o,
  output [15:0] reg_mem_read_data_o,
  output branch_o
);

  Register #(.width(16)) register_1 (.D(data_i), .en(execute_en_i), .clk(clk_i), .Q(data_o), .clr(rst_i));
  Register #(.width(3)) register_2 (.D(adr_reg_d_i), .en(execute_en_i), .clk(clk_i), .Q(adr_reg_d_o), .clr(rst_i));
  Register #(.width(7)) register_3 (
    .D(fetch_ctl_bus_i), .en(execute_en_i), .clk(clk_i), .Q(fetch_ctl_bus_o), .clr(rst_i));
  Register #(.width(5)) register_4 (.D(mem_ctl_bus_i), .en(execute_en_i), .clk(clk_i), .Q(mem_ctl_bus_o), .clr(rst_i));
  Register #(.width(2)) register_5 (
    .D(reg_bank_ctl_bus_i), .en(execute_en_i), .clk(clk_i), .Q(reg_bank_ctl_bus_o), .clr(rst_i));
  Register #(.width(16)) register_6 (.D(lr_addr_i), .en(execute_en_i), .clk(clk_i), .Q(lr_addr_o), .clr(rst_i));
  Register #(.width(1)) register_7 (.D(link_en_i), .en(execute_en_i), .clk(clk_i), .Q(link_en_o), .clr(rst_i));
  Register #(.width(16)) register_8 (
    .D(reg_mem_read_data_i), .en(execute_en_i), .clk(clk_i), .Q(reg_mem_read_data_o), .clr(rst_i));
  Register #(.width(1)) register_9 (.D(branch_i), .en(1'b1), .clk(clk_i), .Q(branch_o), .clr(rst_i));

  assign cpsr_o = cpsr_i;

  // Other names for the same wires on the sheet: clk_s = clk_i; execute_en_s = execute_en_i; rst_s = rst_i

  // Notes on the sheet:
  //   Attention, votre version de Logisim
  //   ne contient pas de tracker. Si vous
  //   enregistrez votre projet, toutes les
  //   informations du tracker seront
  //   définitivement effacées.
endmodule

module mult_2 (
  input  [4:0] imm5_i,
  input  [10:0] offset_incond_i,
  input  [7:0] offset_cond_i,
  input  [2:0] sel_mult_2_i,
  output [15:0] mult_2_out
);

  wire [0:0] offset_cond_ext_signed_incr_x2_s;
  wire [15:0] imm5_ext_unsigned_s, imm5_ext_x2_s, offset_cond_ext_signed_incr_s, offset_cond_ext_signed_s,
       offset_incond_ext_signed_incr_s, offset_incond_ext_signed_incr_x2_s, offset_incond_ext_signed_s,
       offset_incond_ext_signed_shifted_incr_s, offset_incond_ext_signed_shifted_s,
       offset_incond_ext_unsigned_incr_s, offset_incond_ext_unsigned_incr_x2_s, offset_incond_ext_unsigned_s;
  wire [15:1] offset_cond_ext_signed_incr_aligned_s;

  assign imm5_ext_unsigned_s = {{11{1'b0}}, imm5_i};  // Bit_Extender bit_extender_1
  assign offset_incond_ext_signed_s = {{5{offset_incond_i[10]}}, offset_incond_i};  // Bit_Extender bit_extender_2
  assign offset_incond_ext_unsigned_s = {{5{1'b0}}, offset_incond_i};  // Bit_Extender bit_extender_3
  assign offset_cond_ext_signed_s = {{8{offset_cond_i[7]}}, offset_cond_i};  // Bit_Extender bit_extender_4
  Adder #(.width(16)) adder_1 (
    .a(offset_incond_ext_signed_s), .b(16'h1), .out(offset_incond_ext_signed_incr_s), .cin(1'b0));  // open: cout
  Adder #(.width(16)) adder_2 (
    .a(offset_cond_ext_signed_s), .b(16'h1), .out(offset_cond_ext_signed_incr_s), .cin(1'b0));  // open: cout
  Adder #(.width(16)) adder_3 (
    .a(offset_incond_ext_signed_shifted_s), .b(16'h1), .out(offset_incond_ext_signed_shifted_incr_s),
    .cin(1'b0));  // open: cout
  Adder #(.width(16)) adder_4 (
    .a(offset_incond_ext_unsigned_s), .b(16'h1), .out(offset_incond_ext_unsigned_incr_s), .cin(1'b0));  // open: cout
  Shifter #(.width(16)) shifter_1 (.in(imm5_ext_unsigned_s), .\dist (4'b0001), .out(imm5_ext_x2_s));
  Shifter #(.width(16)) shifter_2 (
    .in(offset_incond_ext_signed_incr_s), .\dist (4'b0001), .out(offset_incond_ext_signed_incr_x2_s));
  Shifter #(.width(16)) shifter_3 (
    .in(offset_cond_ext_signed_incr_s), .\dist (4'b0001),
    .out({offset_cond_ext_signed_incr_aligned_s, offset_cond_ext_signed_incr_x2_s[0]}));
  Shifter #(.width(16)) shifter_4 (
    .in(offset_incond_ext_unsigned_incr_s), .\dist (4'b0001), .out(offset_incond_ext_unsigned_incr_x2_s));
  Shifter #(.width(16)) shifter_5 (
    .in(offset_incond_ext_signed_s), .\dist (4'b1100), .out(offset_incond_ext_signed_shifted_s));
  Multiplexer #(.select(3), .width(16), .enable("false")) multiplexer_1 (
    .in0(imm5_ext_x2_s), .in1(offset_incond_ext_signed_incr_x2_s),
    .in2({offset_cond_ext_signed_incr_aligned_s, 1'b0}), .in3(offset_incond_ext_unsigned_incr_x2_s),
    .in4(imm5_ext_unsigned_s), .in5(offset_incond_ext_signed_shifted_s), .in6(offset_incond_ext_unsigned_s),
    .in7({16{1'b0}}), .out(mult_2_out), .sel(sel_mult_2_i));

  // Other names for the same wires on the sheet: imm5_s[4:0] = imm5_i; mult_2_out_s[15:0] = mult_2_out;
  //   offset_cond_ext_signed_incr_x2_s[15:1] = offset_cond_ext_signed_incr_aligned_s;
  //   offset_cond_s[7:0] = offset_cond_i; offset_incond_s[10:0] = offset_incond_i; sel_mult_2_s[2:0] = sel_mult_2_i

  // Notes on the sheet:
  //   Attention, votre version de Logisim
  //   ne contient pas de tracker. Si vous
  //   enregistrez votre projet, toutes les
  //   informations du tracker seront
  //   définitivement effacées.
  //   Extensions nécessaires
  //   Incréments
  //   x2 => shift à gauche = pas de logique
  //   Utilisé pour le BL MSB
  //   Utilisé pour le BL LSB (or logique)
endmodule

module shift (
  input  [15:0] operand_i,
  input  [3:0] sel_shift_data_i,
  input  [2:0] sel_op_shift_i,
  output [15:0] shift_data_out_o
);

  wire [15:0] asr_result_s, lsl_result_s, lsr_result_s, rsr_result_s;

  Shifter #(.width(16), .shift("ar")) shifter_1 (.in(operand_i), .\dist (sel_shift_data_i), .out(asr_result_s));
  Shifter #(.width(16)) shifter_2 (.in(operand_i), .\dist (sel_shift_data_i), .out(lsl_result_s));
  Shifter #(.width(16), .shift("lr")) shifter_3 (.in(operand_i), .\dist (sel_shift_data_i), .out(lsr_result_s));
  Shifter #(.width(16), .shift("rr")) shifter_4 (.in(operand_i), .\dist (sel_shift_data_i), .out(rsr_result_s));
  Multiplexer #(.select(3), .width(16), .enable("false")) multiplexer_1 (
    .in0(operand_i), .in1(asr_result_s), .in2(lsl_result_s), .in3(lsr_result_s), .in4(rsr_result_s),
    .in5({16{1'b0}}), .in6({16{1'b0}}), .in7({16{1'b0}}), .out(shift_data_out_o), .sel(sel_op_shift_i));

  // Other names for the same wires on the sheet: operand_s[15:0] = operand_i; sel_op_shift_s[2:0] = sel_op_shift_i;
  //   sel_shift_data_s[3:0] = sel_shift_data_i

  // Notes on the sheet:
  //   Attention, votre version de Logisim
  //   ne contient pas de tracker. Si vous
  //   enregistrez votre projet, toutes les
  //   informations du tracker seront
  //   définitivement effacées.
endmodule

module alu (
  input  [15:0] operand_1_i,
  input  [15:0] operand_2_i,
  input  [2:0] sel_op_alu_i,
  output [15:0] alu_data_out_o,
  output carry_o,
  output overflow_o
);

  wire adder_1_cout, carry_add_s, carry_sub_s, overflow_add_s, overflow_sub_s, subtractor_1_bout,
       subtractor_2_bout;
  wire [15:0] add_result_s, and_result_s, neg_result_s, not_result_s, or_result_s, sub_result_s, xor_result_s;

  Subtractor #(.width(15)) subtractor_1 (
    .a(operand_1_i[14:0]), .b(operand_2_i[14:0]), .out(sub_result_s[14:0]), .bin(1'b0),
    .bout(subtractor_1_bout));
  Subtractor #(.width(1)) subtractor_2 (
    .a(operand_1_i[15]), .b(operand_2_i[15]), .out(sub_result_s[15]), .bin(subtractor_1_bout),
    .bout(subtractor_2_bout));
  assign and_result_s = operand_1_i & operand_2_i;  // AND_Gate and_1, 16 bits wide
  assign or_result_s = operand_1_i | operand_2_i;  // OR_Gate or_1, 16 bits wide
  assign xor_result_s = operand_1_i ^ operand_2_i;  // XOR_Gate xor_1, 16 bits wide
  assign not_result_s = ~operand_1_i;  // NOT_Gate not_1, 16 bits wide
  Negator #(.width(16)) negator_1 (.in(operand_1_i), .out(neg_result_s));
  Adder #(.width(15)) adder_1 (
    .a(operand_1_i[14:0]), .b(operand_2_i[14:0]), .out(add_result_s[14:0]), .cin(1'b0), .cout(adder_1_cout));
  Adder #(.width(1)) adder_2 (
    .a(operand_1_i[15]), .b(operand_2_i[15]), .out(add_result_s[15]), .cin(adder_1_cout), .cout(carry_add_s));
  xor xor_2 (overflow_add_s, adder_1_cout, carry_add_s);
  xor xor_3 (overflow_sub_s, subtractor_1_bout, subtractor_2_bout);
  not not_2 (carry_sub_s, subtractor_2_bout);
  Multiplexer #(.select(3), .width(16), .enable("false")) multiplexer_1 (
    .in0(operand_1_i), .in1(add_result_s), .in2(sub_result_s), .in3(and_result_s), .in4(or_result_s),
    .in5(not_result_s), .in6(neg_result_s), .in7(xor_result_s), .out(alu_data_out_o), .sel(sel_op_alu_i));
  Multiplexer #(.enable("false")) multiplexer_2 (
    .in0(overflow_sub_s), .in1(overflow_add_s), .out(overflow_o), .sel(sel_op_alu_i[0]));
  Multiplexer #(.enable("false")) multiplexer_3 (
    .in0(carry_sub_s), .in1(carry_add_s), .out(carry_o), .sel(sel_op_alu_i[0]));

  // Other names for the same wires on the sheet: carry_s = carry_o; data_out_s[15:0] = alu_data_out_o;
  //   operand_1_s[15:0] = operand_1_i; operand_2_s[15:0] = operand_2_i; overflow_s = overflow_o;
  //   sel_op_alu_s[2:0] = sel_op_alu_i

  // Notes on the sheet:
  //   Attention, votre version de Logisim
  //   ne contient pas de tracker. Si vous
  //   enregistrez votre projet, toutes les
  //   informations du tracker seront
  //   définitivement effacées.
  //   ALU
  //   Sel OP ALU
endmodule

module zcnv_unit (
  input  [15:0] data_i,
  input  carry_i,
  input  overflow_i,
  output z_o,
  output c_o,
  output n_o,
  output v_o
);

  Comparator #(.width(16)) comparator_1 (.a(data_i), .b({16{1'b0}}), .eq(z_o));  // open: gt, lt

  assign c_o = carry_i;
  assign n_o = data_i[15];
  assign v_o = overflow_i;

  // Other names for the same wires on the sheet: carry_s = carry_i; data_s[15:0] = data_i; overflow_s = overflow_i

  // Notes on the sheet:
  //   Attention, votre version de Logisim
  //   ne contient pas de tracker. Si vous
  //   enregistrez votre projet, toutes les
  //   informations du tracker seront
  //   définitivement effacées.
endmodule

module memory_access (
  input  [15:0] mem_data_i,
  input  [15:0] data_i,
  input  [3:0] cpsr_i,
  input  [2:0] addr_reg_d_i,
  input  [6:0] fetch_ctl_bus_i,
  input  [4:0] mem_ctl_bus_i,
  input  [1:0] reg_bank_ctl_bus_i,
  input  [15:0] lr_addr_i,
  input  link_en_i,
  input  [15:0] reg_mem_read_data_i,
  input  memory_access_en_i,
  input  rst_i,
  input  clk_i,
  output [14:0] mem_data_adr_o,
  output [15:0] mem_adr_byte_o,
  output [15:0] mem_data_out_o,
  output str_data_o,
  output ldr_data_o,
  output high_byte_o,
  output low_byte_o,
  output [15:0] mem_out_o,
  output [2:0] adr_reg_d_o,
  output [1:0] reg_bank_ctl_bus_o,
  output link_en_o,
  output [15:0] lr_addr_o,
  output branch_o
);

  wire and_1_out, and_2_out, and_3_out, condition_tester_1_cond_test_o, not_1_out, not_2_out, or_1_out,
       or_2_out, or_3_out;
  wire [15:0] register_1_q;

  // Probe on data_i
  Multiplexer #(.width(16), .enable("false")) multiplexer_1 (
    .in0(register_1_q), .in1(data_i), .out(mem_adr_byte_o), .sel(or_1_out));
  or or_1 (or_1_out, mem_ctl_bus_i[1], mem_ctl_bus_i[2]);
  Multiplexer #(.width(16), .enable("false")) multiplexer_2 (
    .in0(data_i), .in1(mem_data_i), .out(mem_out_o), .sel(mem_ctl_bus_i[0]));
  Register #(.width(16)) register_1 (
    .D(mem_adr_byte_o), .en(memory_access_en_i), .clk(clk_i), .Q(register_1_q), .clr(rst_i));
  not not_1 (not_1_out, mem_adr_byte_o[0]);
  condition_tester condition_tester_1 (
    .cond_en_i(fetch_ctl_bus_i[1]), .cond_i(fetch_ctl_bus_i[5:2]), .Z_i(cpsr_i[0]), .C_i(cpsr_i[1]),
    .N_i(cpsr_i[2]), .V_i(cpsr_i[3]), .cond_test_o(condition_tester_1_cond_test_o));
  // Probe on register_1_q
  not not_2 (not_2_out, mem_ctl_bus_i[3]);
  and and_1 (and_1_out, mem_ctl_bus_i[3], mem_adr_byte_o[0]);
  and and_2 (and_2_out, mem_ctl_bus_i[3], not_1_out);
  // Probe on reg_mem_read_data_i
  or or_2 (or_2_out, not_2_out, and_1_out);
  or or_3 (or_3_out, not_2_out, and_2_out);
  // Probe on mem_out_o
  and and_3 (and_3_out, fetch_ctl_bus_i[0], condition_tester_1_cond_test_o);
  and and_4 (high_byte_o, memory_access_en_i, or_2_out);
  and and_5 (low_byte_o, memory_access_en_i, or_3_out);
  Multiplexer #(.enable("false")) multiplexer_3 (.in0(1'b0), .in1(and_3_out), .out(branch_o), .sel(memory_access_en_i));

  assign adr_reg_d_o = addr_reg_d_i;
  assign ldr_data_o = mem_ctl_bus_i[2];
  assign link_en_o = link_en_i;
  assign lr_addr_o = lr_addr_i;
  assign mem_data_adr_o = mem_adr_byte_o[15:1];
  assign mem_data_out_o = reg_mem_read_data_i;
  assign reg_bank_ctl_bus_o = reg_bank_ctl_bus_i;
  assign str_data_o = mem_ctl_bus_i[1];

  // Other names for the same wires on the sheet: addr_reg_d_s[2:0] = addr_reg_d_i; cpsr_s[3:0] = cpsr_i;
  //   data_s[15:0] = data_i; fetch_control_bus_s[6:0] = fetch_ctl_bus_i; high_byte_s = high_byte_o;
  //   ldr_addr_s[15:0] = lr_addr_i; link_en_s = link_en_i; low_byte_s = low_byte_o;
  //   mem_adr_byte_s[15:0] = mem_adr_byte_o; mem_data_adr_s[14:0] = mem_adr_byte_o[15:1];
  //   mem_data_s[15:0] = mem_data_i; mem_out_s[15:0] = mem_out_o; memory_access_en_s = memory_access_en_i;
  //   memory_control_bus_s[4:0] = mem_ctl_bus_i; str_data_s = mem_ctl_bus_i[1]; ldr_data_s = mem_ctl_bus_i[2];
  //   reg_bank_ctl_bus_s[1:0] = reg_bank_ctl_bus_i; mem_data_out_s[15:0] = reg_mem_read_data_i;
  //   reg_mem_read_data_s[15:0] = reg_mem_read_data_i

  // Notes on the sheet:
  //   Attention, votre version de Logisim
  //   ne contient pas de tracker. Si vous
  //   enregistrez votre projet, toutes les
  //   informations du tracker seront
  //   définitivement effacées.
  //   Entité MEMORY ACCESS
  //   sel_PC
  //   cond_en_s
  //   cond_s
  //   sel_mem_s
  //   byte_s
  //   address_offset_s
  //   cond_test_s
  //   branch_s
endmodule

module memory_bank_reg (
  input  [15:0] mem_out_i,
  input  [2:0] addr_reg_d_i,
  input  [1:0] reg_bank_ctl_bus_i,
  input  link_en_i,
  input  [15:0] ldr_addr_i,
  input  memory_access_en_i,
  input  clk_i,
  input  rst_i,
  output [15:0] mem_out_o,
  output [2:0] addr_reg_d_o,
  output [1:0] reg_bank_ctl_bus_o,
  output link_en_o,
  output [15:0] ldr_addr_o
);

  Register #(.width(16)) register_1 (.D(mem_out_i), .en(memory_access_en_i), .clk(clk_i), .Q(mem_out_o), .clr(rst_i));
  Register #(.width(3)) register_2 (
    .D(addr_reg_d_i), .en(memory_access_en_i), .clk(clk_i), .Q(addr_reg_d_o), .clr(rst_i));
  Register #(.width(2)) register_3 (
    .D(reg_bank_ctl_bus_i), .en(memory_access_en_i), .clk(clk_i), .Q(reg_bank_ctl_bus_o), .clr(rst_i));
  Register #(.width(1)) register_4 (.D(link_en_i), .en(memory_access_en_i), .clk(clk_i), .Q(link_en_o), .clr(rst_i));
  Register #(.width(16)) register_5 (.D(ldr_addr_i), .en(memory_access_en_i), .clk(clk_i), .Q(ldr_addr_o), .clr(rst_i));

  // Other names for the same wires on the sheet: memory_access_en_s = memory_access_en_i

  // Notes on the sheet:
  //   Attention, votre version de Logisim
  //   ne contient pas de tracker. Si vous
  //   enregistrez votre projet, toutes les
  //   informations du tracker seront
  //   définitivement effacées.
endmodule

module hazard_detection (
  input  instr_control_i,
  input  reg_bank_write_en_i,
  input  [2:0] adr_reg_d_i,
  input  [2:0] adr_reg_n_i,
  input  [2:0] adr_reg_m_i,
  input  [2:0] adr_reg_mem_i,
  input  reg_n_en_i,
  input  reg_m_en_i,
  input  reg_mem_en_i,
  input  sel_mem_i,
  input  branch_i,
  input  clk_i,
  input  rst_i,
  output fetch_en_o,
  output decode_en_o,
  output execute_en_o,
  output memory_en_o,
  output bank_register_en,
  output [1:0] sel_op2_forward_o,
  output [1:0] sel_op1_forward_o,
  output [1:0] sel_op_mem_forward_o
);

  wire no_ctl_hazard_s, no_data_hazard_s;

  control_hazard control_hazard_1 (
    .no_data_hazard_i(no_data_hazard_s), .instr_control_i(instr_control_i), .clk_i(clk_i), .rst_i(rst_i),
    .no_ctl_hazard_o(no_ctl_hazard_s));
  data_hazard data_hazard_1 (
    .reg_bank_write_en_i(reg_bank_write_en_i), .adr_reg_d_i(adr_reg_d_i), .adr_reg_n_i(adr_reg_n_i),
    .adr_reg_m_i(adr_reg_m_i), .adr_reg_mem_i(adr_reg_mem_i), .reg_n_en_i(reg_n_en_i),
    .reg_m_en_i(reg_m_en_i), .reg_mem_en_i(reg_mem_en_i), .sel_mem_i(sel_mem_i), .decode_en_i(decode_en_o),
    .execute_en_i(execute_en_o), .mem_access_en_i(memory_en_o), .reg_bank_en_i(bank_register_en),
    .clk_i(clk_i), .rst_i(rst_i), .no_data_hazard_o(no_data_hazard_s), .sel_op1_forward_o(sel_op1_forward_o),
    .sel_op2_forward_o(sel_op2_forward_o), .sel_op_mem_forward_o(sel_op_mem_forward_o));
  Register #(.width(1)) register_1 (.D(decode_en_o), .en(1'b1), .clk(clk_i), .Q(execute_en_o), .clr(rst_i));
  and and_1 (decode_en_o, no_data_hazard_s, ~branch_i, no_ctl_hazard_s);  // AND_Gate
  and and_2 (fetch_en_o, no_ctl_hazard_s, no_data_hazard_s);
  Register #(.width(1)) register_2 (.D(execute_en_o), .en(1'b1), .clk(clk_i), .Q(memory_en_o), .clr(rst_i));
  Register #(.width(1)) register_3 (.D(memory_en_o), .en(1'b1), .clk(clk_i), .Q(bank_register_en), .clr(rst_i));

  // Other names for the same wires on the sheet: branch_s = branch_i; clk_s = clk_i; decode_en_s = decode_en_o;
  //   execute_en_s = execute_en_o; fetch_en_s = fetch_en_o; mem_access_en_s = memory_en_o;
  //   reg_bank_en_s = bank_register_en; rst_s = rst_i; sel_op1_forward_s[1:0] = sel_op1_forward_o;
  //   sel_op2_forward_s[1:0] = sel_op2_forward_o; sel_op_mem_forward_s[1:0] = sel_op_mem_forward_o

  // Notes on the sheet:
  //   Attention, votre version de Logisim
  //   ne contient pas de tracker. Si vous
  //   enregistrez votre projet, toutes les
  //   informations du tracker seront
  //   définitivement effacées.
endmodule

module control_hazard (
  input  no_data_hazard_i,
  input  instr_control_i,
  input  clk_i,
  input  rst_i,
  output no_ctl_hazard_o
);

  wire and_1_out, and_2_out, d_ff_1_q, d_ff_2_q, d_ff_3_q, multiplexer_1_out, not_1_out;

  and and_1 (and_1_out, no_data_hazard_i, instr_control_i);
  not not_1 (not_1_out, and_1_out);
  Multiplexer #(.enable("false")) multiplexer_1 (.in0(and_1_out), .in1(1'b0), .out(multiplexer_1_out), .sel(and_2_out));
  D_Flip_Flop d_ff_1 (.D(multiplexer_1_out), .clk(clk_i), .Q(d_ff_1_q), .reset(rst_i));  // open: Qn, preset
  D_Flip_Flop d_ff_2 (.D(d_ff_1_q), .clk(clk_i), .Q(d_ff_2_q), .reset(rst_i));  // open: Qn, preset
  D_Flip_Flop d_ff_3 (.D(d_ff_2_q), .clk(clk_i), .Q(d_ff_3_q), .reset(rst_i));  // open: Qn, preset
  and and_2 (and_2_out, d_ff_1_q, d_ff_2_q, d_ff_3_q);
  or or_1 (no_ctl_hazard_o, not_1_out, and_2_out);

  // Other names for the same wires on the sheet: clk_s = clk_i; rst_s = rst_i

  // Notes on the sheet:
  //   Attention, votre version de Logisim
  //   ne contient pas de tracker. Si vous
  //   enregistrez votre projet, toutes les
  //   informations du tracker seront
  //   définitivement effacées.
  //   no_ctl_hazard should be 1 again after 3 clocks
  //   no_ctl_hazard becomes zero immediatly when instr_control_i = 1
  //   And no_ctl_hazard is keep at zero for 3 clocks if no_data_hazard = 1
endmodule

module data_hazard (
  input  reg_bank_write_en_i,
  input  [2:0] adr_reg_d_i,
  input  [2:0] adr_reg_n_i,
  input  [2:0] adr_reg_m_i,
  input  [2:0] adr_reg_mem_i,
  input  reg_n_en_i,
  input  reg_m_en_i,
  input  reg_mem_en_i,
  input  sel_mem_i,
  input  decode_en_i,
  input  execute_en_i,
  input  mem_access_en_i,
  input  reg_bank_en_i,
  input  clk_i,
  input  rst_i,
  output no_data_hazard_o,
  output [1:0] sel_op1_forward_o,
  output [1:0] sel_op2_forward_o,
  output [1:0] sel_op_mem_forward_o
);

  wire and_10_out, and_11_out, and_12_out, and_13_out, and_14_out, and_15_out, and_16_out, and_17_out,
       and_18_out, comparator_1_eq, comparator_2_eq, comparator_3_eq, comparator_4_eq, comparator_5_eq,
       comparator_6_eq, comparator_7_eq, comparator_8_eq, comparator_9_eq, exec_write_en_s, execute_m,
       execute_mem, execute_n, mem_write_en_s, memory_m, memory_mem, memory_n, reg_m_hazard_s,
       reg_mem_hazard_s, reg_n_hazard_s, sel_mem_exec, sel_mem_mem, sel_mem_wb, write_back_write_en_s,
       write_m, write_mem, write_n;
  wire [2:0] exec_reg_s, mem_reg_s, write_back_reg_s;

  Comparator #(.width(3), .mode("unsigned")) comparator_1 (
    .a(exec_reg_s), .b(adr_reg_n_i), .eq(comparator_1_eq));  // open: gt, lt
  Comparator #(.width(3), .mode("unsigned")) comparator_2 (
    .a(mem_reg_s), .b(adr_reg_n_i), .eq(comparator_2_eq));  // open: gt, lt
  Comparator #(.width(3), .mode("unsigned")) comparator_3 (
    .a(write_back_reg_s), .b(adr_reg_n_i), .eq(comparator_3_eq));  // open: gt, lt
  Comparator #(.width(3), .mode("unsigned")) comparator_4 (
    .a(exec_reg_s), .b(adr_reg_m_i), .eq(comparator_4_eq));  // open: gt, lt
  Comparator #(.width(3), .mode("unsigned")) comparator_5 (
    .a(mem_reg_s), .b(adr_reg_m_i), .eq(comparator_5_eq));  // open: gt, lt
  Comparator #(.width(3), .mode("unsigned")) comparator_6 (
    .a(write_back_reg_s), .b(adr_reg_m_i), .eq(comparator_6_eq));  // open: gt, lt
  Comparator #(.width(3), .mode("unsigned")) comparator_7 (
    .a(exec_reg_s), .b(adr_reg_mem_i), .eq(comparator_7_eq));  // open: gt, lt
  Comparator #(.width(3), .mode("unsigned")) comparator_8 (
    .a(mem_reg_s), .b(adr_reg_mem_i), .eq(comparator_8_eq));  // open: gt, lt
  Comparator #(.width(3), .mode("unsigned")) comparator_9 (
    .a(write_back_reg_s), .b(adr_reg_mem_i), .eq(comparator_9_eq));  // open: gt, lt
  and and_1 (execute_n, reg_n_en_i, comparator_1_eq, exec_write_en_s, execute_en_i);
  and and_2 (memory_n, reg_n_en_i, comparator_2_eq, mem_write_en_s, mem_access_en_i);
  and and_3 (write_n, reg_n_en_i, comparator_3_eq, write_back_write_en_s, reg_bank_en_i);
  and and_4 (execute_m, reg_m_en_i, comparator_4_eq, exec_write_en_s, execute_en_i);
  and and_5 (memory_m, reg_m_en_i, comparator_5_eq, mem_write_en_s, mem_access_en_i);
  and and_6 (write_m, reg_m_en_i, comparator_6_eq, write_back_write_en_s, reg_bank_en_i);
  and and_7 (execute_mem, reg_mem_en_i, comparator_7_eq, exec_write_en_s, execute_en_i);
  and and_8 (memory_mem, reg_mem_en_i, comparator_8_eq, mem_write_en_s, mem_access_en_i);
  and and_9 (write_mem, reg_mem_en_i, comparator_9_eq, write_back_write_en_s, reg_bank_en_i);
  or or_1 (reg_n_hazard_s, execute_n, memory_n, write_n);
  or or_2 (reg_m_hazard_s, execute_m, memory_m, write_m);
  or or_3 (reg_mem_hazard_s, execute_mem, memory_mem, write_mem);
  Register #(.width(1)) register_1 (.D(sel_mem_i), .en(1'b1), .clk(clk_i), .Q(sel_mem_exec), .clr(rst_i));
  Register #(.width(3)) register_2 (.D(adr_reg_d_i), .en(1'b1), .clk(clk_i), .Q(exec_reg_s), .clr(rst_i));
  Register #(.width(1)) register_3 (.D(reg_bank_write_en_i), .en(1'b1), .clk(clk_i), .Q(exec_write_en_s), .clr(rst_i));
  nor nor_1 (no_data_hazard_o, reg_n_hazard_s, reg_m_hazard_s, reg_mem_hazard_s);
  Register #(.width(1)) register_4 (.D(sel_mem_exec), .en(1'b1), .clk(clk_i), .Q(sel_mem_mem), .clr(rst_i));
  Register #(.width(3)) register_5 (.D(exec_reg_s), .en(1'b1), .clk(clk_i), .Q(mem_reg_s), .clr(rst_i));
  Register #(.width(1)) register_6 (.D(exec_write_en_s), .en(1'b1), .clk(clk_i), .Q(mem_write_en_s), .clr(rst_i));
  Register #(.width(1)) register_7 (.D(sel_mem_mem), .en(1'b1), .clk(clk_i), .Q(sel_mem_wb), .clr(rst_i));
  Register #(.width(3)) register_8 (.D(mem_reg_s), .en(1'b1), .clk(clk_i), .Q(write_back_reg_s), .clr(rst_i));
  Register #(.width(1)) register_9 (.D(mem_write_en_s), .en(1'b1), .clk(clk_i), .Q(write_back_write_en_s), .clr(rst_i));
  and and_10 (and_10_out, execute_n, ~sel_mem_exec);  // AND_Gate
  or or_4 (sel_op1_forward_o[0], and_10_out, and_11_out);
  and and_11 (and_11_out, write_n, ~sel_mem_wb);  // AND_Gate
  or or_5 (sel_op1_forward_o[1], and_11_out, and_12_out);
  and and_12 (and_12_out, memory_n, ~sel_mem_mem);  // AND_Gate
  and and_13 (and_13_out, execute_m, ~sel_mem_exec);  // AND_Gate
  or or_6 (sel_op2_forward_o[0], and_13_out, and_14_out);
  and and_14 (and_14_out, write_m, ~sel_mem_wb);  // AND_Gate
  or or_7 (sel_op2_forward_o[1], and_14_out, and_15_out);
  and and_15 (and_15_out, memory_m, ~sel_mem_mem);  // AND_Gate
  and and_16 (and_16_out, execute_mem, ~sel_mem_exec);  // AND_Gate
  or or_8 (sel_op_mem_forward_o[0], and_16_out, and_17_out);
  and and_17 (and_17_out, write_mem, ~sel_mem_wb);  // AND_Gate
  or or_9 (sel_op_mem_forward_o[1], and_17_out, and_18_out);
  and and_18 (and_18_out, memory_mem, ~sel_mem_mem);  // AND_Gate

  // Other names for the same wires on the sheet: adr_reg_d_s[2:0] = adr_reg_d_i; adr_reg_m_s[2:0] = adr_reg_m_i;
  //   adr_reg_mem_s[2:0] = adr_reg_mem_i; adr_reg_n_s[2:0] = adr_reg_n_i; clk_s = clk_i; decode_en_s = decode_en_i;
  //   execute_en_s = execute_en_i; mem_access_en_s = mem_access_en_i; no_data_hazard_s = no_data_hazard_o;
  //   reg_bank_en_s = reg_bank_en_i; reg_bank_write_en_s = reg_bank_write_en_i; reg_m_en_s = reg_m_en_i;
  //   reg_mem_en_s = reg_mem_en_i; reg_n_en_s = reg_n_en_i; rst_s = rst_i; sel_mem_s = sel_mem_i

  // Notes on the sheet:
  //   Attention, votre version de Logisim
  //   ne contient pas de tracker. Si vous
  //   enregistrez votre projet, toutes les
  //   informations du tracker seront
  //   définitivement effacées.
  //   a data hazard happens if all these conditions are true:
  //   The register that is equal is valid (reg_en) otherwise the register is used (not read)
  //   The stage of where the instruction is, is enabled (otherwise the write will not happen)
  //   If the write_en of the instruction in respectively execute, mem_access or write_back is 1 (otherwise the register is not written)
  //   a register that a read (n/m/mem) of the instruction in block decode is equal to the register that is written for the instruction in block execute, memory_access or write_back
  //   Save the write register address to know its value for the instruction that is in the execute, memory_access or write_back stage
  //   Save the reg_bank_write_en bit to know if the instruction in the execute, memory_access or write_back stage will perform a write in a register
  //   Data hazard is solved if forwarding is possible (sel_op_forward != 0)
endmodule
